// Logisim project cpu_3.3.circ as structural Verilog: 30 circuits, main circuit cpu_v3
module main (
  input  in_1,
  input  operation_mode,
  input  [7:0] data,
  input  [7:0] instruction,
  input  [7:0] adress,
  input  in_6,
  output [7:0] out_7,
  output [7:0] out_8,
  output [7:0] out_9,
  output [7:0] out_10,
  output out_11
);

  wire adress_decoder_adress_0, adress_decoder_adress_1, adress_decoder_adress_2, adress_decoder_adress_3,
       and_1_out, and_2_out, and_3_out, greater_equal_zero_out, greater_zero_out,
       Instruction_decoder_addition, Instruction_decoder_equals_zweo, Instruction_decoder_greater_equal_zero,
       Instruction_decoder_greater_zero, Instruction_decoder_not_zero,
       Instruction_decoder_smaller_equal_zero, Instruction_decoder_smaller_zero,
       Instruction_decoder_subtraction, nor_1_out, nor_2_out, nor_3_out, not_1_out, not_2_out, not_3_out,
       not_zero_out, or_1_out, or_2_out, or_3_out, or_4_out, or_5_out, or_6_out, or_7_out, or_8_out,
       or_9_out, or_10_out, or_11_out, or_12_out, or_13_out, or_14_out, reg_to_bus_1_o,
       smaller_equal_zero_out, smaller_zero_out, sys_clock_out, zero_out;
  wire [0:0] comperator_out_out;
  wire [7:0] byte_inverter_1_out_2, byte_mux_1_out_4, byte_mux_2_out_4, byte_mux_3_out_4, byte_mux_4_out_4,
       byte_mux_5_out_4, byte_mux_6_out_4, byte_mux_7_out_4, byte_switch_2_o, byte_switch_3_o,
       byte_switch_4_o, byte_switch_5_o, byte_switch_6_o, byte_switch_7_o, byter_adder_1_o_1, counter_1_q,
       instruction_ROM_data, mux_4_byte_2_p6, reg_0_q, reg_1_q, reg_2_q, reg_3_q, rom_1_data;

  Counter counter_1 (.Q(counter_1_q), .clk(and_1_out));  // open: load, D, count, carry, up, clr
  ROM rom_1 (.addr(counter_1_q), .data(rom_1_data));
  ROM instruction_ROM (.addr(counter_1_q), .data(instruction_ROM_data));
  Byte_MUX byte_mux_1 (.select_input(operation_mode), .in_0(instruction), .in_1(rom_1_data), .out_4(byte_mux_1_out_4));
  Byte_MUX byte_mux_2 (
    .select_input(operation_mode), .in_0(adress), .in_1(instruction_ROM_data), .out_4(byte_mux_2_out_4));
  not not_1 (not_1_out, byte_mux_1_out_4[6]);
  and and_1 (and_1_out, not_1_out, sys_clock_out);
  Byte_MUX byte_mux_3 (.select_input(reg_to_bus_1_o), .in_0(data), .in_1(out_8), .out_4(byte_mux_3_out_4));
  reg_to_bus reg_to_bus_1 (.bus_in(byte_mux_1_out_4), .o(reg_to_bus_1_o));
  Clock sys_clock (.out(sys_clock_out));
  and and_2 (and_2_out, in_1, 1'b1);
  Byte_switch byte_switch_1 (.i(byte_mux_3_out_4), .switch(and_2_out), .o(out_7));
  Byte_switch byte_switch_2 (.i(byte_mux_1_out_4), .switch(and_2_out), .o(byte_switch_2_o));
  Byte_switch byte_switch_3 (.i(byte_mux_2_out_4), .switch(and_2_out), .o(byte_switch_3_o));
  Byte_MUX byte_mux_4 (
    .select_input(byte_switch_2_o[1]), .in_0(byte_mux_3_out_4), .in_1(mux_4_byte_2_p6),
    .out_4(byte_mux_4_out_4));
  Adress_dcoder adress_decoder (
    .in_1(byte_switch_3_o), .adress_0(adress_decoder_adress_0), .adress_1(adress_decoder_adress_1),
    .adress_2(adress_decoder_adress_2), .adress_3(adress_decoder_adress_3));
  or or_1 (or_1_out, or_2_out, adress_decoder_adress_3);
  Byte_MUX byte_mux_5 (
    .select_input(or_2_out), .in_0(byte_mux_4_out_4), .in_1(byte_mux_7_out_4), .out_4(byte_mux_5_out_4));
  Register reg_0 (.D(byte_mux_4_out_4), .en(adress_decoder_adress_0), .clk(sys_clock_out), .Q(reg_0_q));  // open: clr
  Register reg_1 (.D(byte_mux_4_out_4), .en(adress_decoder_adress_1), .clk(sys_clock_out), .Q(reg_1_q));  // open: clr
  Register reg_2 (.D(byte_mux_4_out_4), .en(adress_decoder_adress_2), .clk(sys_clock_out), .Q(reg_2_q));  // open: clr
  Register reg_3 (.D(byte_mux_5_out_4), .en(or_1_out), .clk(sys_clock_out), .Q(reg_3_q));  // open: clr
  // MUX_4_Byte mux_4_byte_1: pin names not known; wires that end beside it: byte_switch_3_o, reg_0_q, reg_1_q, reg_2_q, reg_3_q, byte_switch_3_o, out_8
  // MUX_4_Byte mux_4_byte_2: pin names not known; wires that end beside it: byte_switch_3_o, reg_0_q, reg_1_q, reg_2_q, reg_3_q, mux_4_byte_2_p6
  LedBar ledbar_1 (
    .led0(out_7[7]), .led1(out_7[6]), .led2(out_7[5]), .led3(out_7[4]), .led4(out_7[3]), .led5(out_7[2]),
    .led6(out_7[1]), .led7(out_7[0]));
  alu_decoder Instruction_decoder (
    .instruction_Bus_in(byte_switch_2_o), .greater_equal_zero(Instruction_decoder_greater_equal_zero),
    .smaller_equal_zero(Instruction_decoder_smaller_equal_zero),
    .subtraction(Instruction_decoder_subtraction), .addition(Instruction_decoder_addition),
    .equals_zweo(Instruction_decoder_equals_zweo), .not_zero(Instruction_decoder_not_zero),
    .greater_zero(Instruction_decoder_greater_zero), .smaller_zero(Instruction_decoder_smaller_zero));
  Byte_switch byte_switch_4 (.i(reg_1_q), .switch(Instruction_decoder_addition), .o(byte_switch_4_o));
  Byte_switch byte_switch_5 (.i(reg_2_q), .switch(Instruction_decoder_addition), .o(byte_switch_5_o));
  or or_2 (or_2_out, Instruction_decoder_addition, Instruction_decoder_subtraction, or_3_out);
  Byte_switch byte_switch_6 (.i(reg_1_q), .switch(Instruction_decoder_subtraction), .o(byte_switch_6_o));
  Byte_inverter byte_inverter_1 (.in_1(byte_switch_7_o), .out_2(byte_inverter_1_out_2));
  Byte_switch byte_switch_7 (.i(reg_2_q), .switch(Instruction_decoder_subtraction), .o(byte_switch_7_o));
  Byter_adder addition (.i_1(byte_switch_4_o), .i_2(byte_switch_5_o), .o_1(out_10), .carry(out_11));
  Byte_MUX byte_mux_6 (
    .select_input(Instruction_decoder_addition), .in_0(out_9), .in_1(out_10), .out_4(byte_mux_6_out_4));
  Byte_MUX byte_mux_7 (
    .select_input(not_2_out), .in_0({{7{in_6}}, comperator_out_out[0]}), .in_1(byte_mux_6_out_4),
    .out_4(byte_mux_7_out_4));
  not not_2 (not_2_out, or_3_out);
  Byter_adder byter_adder_1 (.i_1(byte_inverter_1_out_2), .i_2(8'h1), .o_1(byter_adder_1_o_1));  // open: carry
  or or_3 (or_3_out, Instruction_decoder_smaller_equal_zero, Instruction_decoder_greater_equal_zero, or_4_out);
  or or_4 (or_4_out, Instruction_decoder_smaller_zero, Instruction_decoder_greater_zero, Instruction_decoder_not_zero, Instruction_decoder_equals_zweo);
  Byter_adder subtraction (.i_1(byte_switch_6_o), .i_2(byter_adder_1_o_1), .o_1(out_9));  // open: carry
  or or_5 (or_5_out, Instruction_decoder_greater_zero, or_3_out);
  not not_3 (not_3_out, out_7[7]);
  nor nor_1 (nor_1_out, out_7[0], out_7[1], out_7[2], out_7[3]);
  nor nor_2 (nor_2_out, out_7[4], out_7[5], out_7[6], out_7[7]);
  or or_6 (or_6_out, Instruction_decoder_smaller_zero, or_3_out);
  and comperator_out (comperator_out_out[0], or_3_out, or_11_out);
  and zero (zero_out, Instruction_decoder_equals_zweo, nor_1_out, nor_2_out);
  nor nor_3 (nor_3_out, nor_1_out, nor_2_out);
  or or_7 (or_7_out, out_7[0], out_7[1], out_7[2]);
  or or_8 (or_8_out, or_7_out, or_9_out);
  or or_9 (or_9_out, out_7[3], out_7[4], out_7[5], out_7[6]);
  and and_3 (and_3_out, out_7[7], or_8_out);
  or or_10 (or_10_out, out_7[7], and_3_out);
  and not_zero (not_zero_out, Instruction_decoder_not_zero, nor_3_out);
  and greater_zero (greater_zero_out, or_5_out, or_8_out, not_3_out);
  and smaller_zero (smaller_zero_out, or_10_out, or_6_out);
  or or_11 (or_11_out, smaller_zero_out, smaller_equal_zero_out, zero_out, or_14_out);
  or or_12 (or_12_out, greater_zero_out, zero_out);
  and greater_equal_zero (greater_equal_zero_out, or_12_out, Instruction_decoder_greater_equal_zero);
  or or_13 (or_13_out, smaller_zero_out, zero_out);
  and smaller_equal_zero (smaller_equal_zero_out, or_13_out, Instruction_decoder_smaller_equal_zero);
  or or_14 (or_14_out, greater_equal_zero_out, greater_zero_out, not_zero_out);

  // Notes on the sheet:
  //   contents of rom_1 (hex, n*v repeats v):
  //   1 2 6 43
  //   contents of instruction_ROM (hex, n*v repeats v):
  //   20 32 0 4
  //   0 = manual
  //   write
  //   |
  //   read
  //   stop_Rom
  //   activate
  //   Data Bus
  //   Instruction Bus
  //   Adress Bus
  //   input selecter
endmodule

module full_adder (
  input  A,
  input  B,
  input  C_in_6a097d25,
  output sum,
  output count
);

  wire and_1_out, and_2_out, xor_1_out;

  xor xor_1 (xor_1_out, A, B);
  and and_1 (and_1_out, A, B);
  xor xor_2 (sum, xor_1_out, C_in_6a097d25);
  and and_2 (and_2_out, xor_1_out, C_in_6a097d25);
  or or_1 (count, and_2_out, and_1_out);
endmodule

module Gated_Latch (
  input  set,
  input  reset,
  output out_3
);

  wire and_1_out, and_2_out, not_1_out, not_2_out, or_1_out;

  not not_1 (not_1_out, set);
  and and_1 (and_1_out, set, reset);
  and and_2 (and_2_out, not_1_out, reset);
  or or_1 (or_1_out, out_3, and_1_out);
  not not_2 (not_2_out, and_2_out);
  and and_3 (out_3, or_1_out, not_2_out);
endmodule

module Byte_register (
  input  clock_in,
  input  enable_write,
  input  [7:0] data_in,
  output [7:0] data_out
);

  wire and_1_out, and_2_out, and_3_out, and_4_out, and_5_out, and_6_out, and_7_out, and_8_out, and_9_out,
       and_10_out, and_11_out, and_12_out, and_13_out, and_14_out, and_15_out, and_16_out, and_17_out,
       not_1_out, not_2_out, not_3_out, not_4_out, not_5_out, not_6_out, not_7_out, not_8_out, not_9_out,
       not_10_out, not_11_out, not_12_out, not_13_out, not_14_out, not_15_out, not_16_out, or_1_out,
       or_2_out, or_3_out, or_4_out, or_5_out, or_6_out, or_7_out, or_8_out;

  and and_1 (and_1_out, enable_write, clock_in);
  not not_1 (not_1_out, data_in[0]);
  not not_2 (not_2_out, data_in[1]);
  not not_3 (not_3_out, data_in[2]);
  not not_4 (not_4_out, data_in[3]);
  not not_5 (not_5_out, data_in[4]);
  not not_6 (not_6_out, data_in[5]);
  not not_7 (not_7_out, data_in[6]);
  not not_8 (not_8_out, data_in[7]);
  and and_2 (and_2_out, data_in[0], and_1_out);
  and and_3 (and_3_out, not_1_out, and_1_out);
  and and_4 (and_4_out, data_in[1], and_1_out);
  and and_5 (and_5_out, not_2_out, and_1_out);
  and and_6 (and_6_out, data_in[2], and_1_out);
  and and_7 (and_7_out, not_3_out, and_1_out);
  and and_8 (and_8_out, data_in[3], and_1_out);
  and and_9 (and_9_out, not_4_out, and_1_out);
  and and_10 (and_10_out, data_in[4], and_1_out);
  and and_11 (and_11_out, not_5_out, and_1_out);
  and and_12 (and_12_out, data_in[5], and_1_out);
  and and_13 (and_13_out, not_6_out, and_1_out);
  and and_14 (and_14_out, data_in[6], and_1_out);
  and and_15 (and_15_out, not_7_out, and_1_out);
  and and_16 (and_16_out, data_in[7], and_1_out);
  and and_17 (and_17_out, not_8_out, and_1_out);
  or or_1 (or_1_out, data_out[0], and_2_out);
  not not_9 (not_9_out, and_3_out);
  or or_2 (or_2_out, data_out[1], and_4_out);
  not not_10 (not_10_out, and_5_out);
  or or_3 (or_3_out, data_out[2], and_6_out);
  not not_11 (not_11_out, and_7_out);
  or or_4 (or_4_out, data_out[3], and_8_out);
  not not_12 (not_12_out, and_9_out);
  or or_5 (or_5_out, data_out[4], and_10_out);
  not not_13 (not_13_out, and_11_out);
  or or_6 (or_6_out, data_out[5], and_12_out);
  not not_14 (not_14_out, and_13_out);
  or or_7 (or_7_out, data_out[6], and_14_out);
  not not_15 (not_15_out, and_15_out);
  or or_8 (or_8_out, data_out[7], and_16_out);
  not not_16 (not_16_out, and_17_out);
  and and_18 (data_out[0], or_1_out, not_9_out);
  and and_19 (data_out[1], or_2_out, not_10_out);
  and and_20 (data_out[2], or_3_out, not_11_out);
  and and_21 (data_out[3], or_4_out, not_12_out);
  and and_22 (data_out[4], or_5_out, not_13_out);
  and and_23 (data_out[5], or_6_out, not_14_out);
  and and_24 (data_out[6], or_7_out, not_15_out);
  and and_25 (data_out[7], or_8_out, not_16_out);
endmodule

module decoder_2_bit (
  input  in_1_2c4f912e,
  input  in_2_2398e526,
  output out_1_367624e9,
  output out_2_0610cceb,
  output out_3_f383ddb4,
  output out_4_fdb79afc
);

  wire not_1_out, not_2_out;

  not not_1 (not_1_out, in_1_2c4f912e);
  not not_2 (not_2_out, in_2_2398e526);
  nor nor_1 (out_1_367624e9, in_1_2c4f912e, in_2_2398e526);
  and and_1 (out_2_0610cceb, not_1_out, in_2_2398e526);
  and and_2 (out_3_f383ddb4, in_1_2c4f912e, not_2_out);
  and and_3 (out_4_fdb79afc, in_1_2c4f912e, in_2_2398e526);
endmodule

module adress_memory_16_bit (
  input  write_1,
  input  write_2,
  input  write_3,
  input  write_4,
  input  read_1,
  input  read_2,
  input  read_3,
  input  read_4,
  input  enable_read,
  input  enable_write,
  input  input_value,
  output output_value
);

  wire and_1_out, and_2_out, and_3_out, and_4_out, and_5_out, and_6_out, and_7_out, and_8_out, and_9_out,
       and_10_out, and_11_out, and_12_out, and_13_out, and_14_out, and_15_out, and_16_out, and_17_out,
       and_18_out, and_19_out, and_20_out, and_21_out, and_22_out, and_23_out, and_24_out, and_25_out,
       and_26_out, and_27_out, and_28_out, and_29_out, and_30_out, and_31_out, and_32_out, and_33_out,
       and_34_out, and_35_out, and_36_out, and_37_out, and_38_out, and_39_out, and_40_out, and_41_out,
       and_42_out, and_43_out, and_44_out, and_45_out, and_46_out, and_47_out, and_48_out, and_49_out,
       and_50_out, and_51_out, and_52_out, and_53_out, and_54_out, and_55_out, and_56_out, and_57_out,
       and_58_out, and_59_out, and_60_out, and_61_out, and_62_out, and_63_out, and_64_out, and_65_out,
       and_66_out, and_67_out, and_68_out, and_69_out, and_70_out, and_71_out, and_72_out, and_73_out,
       and_74_out, and_75_out, and_76_out, and_77_out, and_78_out, and_79_out, and_80_out,
       decoder_2_bit_1_out_1_367624e9, decoder_2_bit_1_out_2_0610cceb, decoder_2_bit_1_out_3_f383ddb4,
       decoder_2_bit_1_out_4_fdb79afc, decoder_2_bit_2_out_1_367624e9, decoder_2_bit_2_out_2_0610cceb,
       decoder_2_bit_2_out_3_f383ddb4, decoder_2_bit_2_out_4_fdb79afc, decoder_2_bit_3_out_1_367624e9,
       decoder_2_bit_3_out_2_0610cceb, decoder_2_bit_3_out_3_f383ddb4, decoder_2_bit_3_out_4_fdb79afc,
       decoder_2_bit_4_out_1_367624e9, decoder_2_bit_4_out_2_0610cceb, decoder_2_bit_4_out_3_f383ddb4,
       decoder_2_bit_4_out_4_fdb79afc, gated_latch_1_out_3, gated_latch_2_out_3, gated_latch_3_out_3,
       gated_latch_4_out_3, gated_latch_5_out_3, gated_latch_6_out_3, gated_latch_7_out_3,
       gated_latch_8_out_3, gated_latch_9_out_3, gated_latch_10_out_3, gated_latch_11_out_3,
       gated_latch_12_out_3, gated_latch_13_out_3, gated_latch_14_out_3, gated_latch_15_out_3,
       gated_latch_16_out_3, or_1_out, or_2_out, or_3_out, or_4_out, or_5_out, or_6_out, or_7_out, or_8_out,
       or_9_out, or_10_out, or_11_out, or_12_out, or_13_out, or_14_out, or_15_out, or_16_out, or_17_out,
       or_18_out, or_19_out, or_20_out, or_21_out, or_22_out;

  decoder_2_bit decoder_2_bit_1 (
    .in_1_2c4f912e(write_1), .in_2_2398e526(write_2), .out_1_367624e9(decoder_2_bit_1_out_1_367624e9),
    .out_2_0610cceb(decoder_2_bit_1_out_2_0610cceb), .out_3_f383ddb4(decoder_2_bit_1_out_3_f383ddb4),
    .out_4_fdb79afc(decoder_2_bit_1_out_4_fdb79afc));
  decoder_2_bit decoder_2_bit_2 (
    .in_1_2c4f912e(write_3), .in_2_2398e526(write_4), .out_1_367624e9(decoder_2_bit_2_out_1_367624e9),
    .out_2_0610cceb(decoder_2_bit_2_out_2_0610cceb), .out_3_f383ddb4(decoder_2_bit_2_out_3_f383ddb4),
    .out_4_fdb79afc(decoder_2_bit_2_out_4_fdb79afc));
  decoder_2_bit decoder_2_bit_3 (
    .in_1_2c4f912e(read_1), .in_2_2398e526(read_2), .out_1_367624e9(decoder_2_bit_3_out_1_367624e9),
    .out_2_0610cceb(decoder_2_bit_3_out_2_0610cceb), .out_3_f383ddb4(decoder_2_bit_3_out_3_f383ddb4),
    .out_4_fdb79afc(decoder_2_bit_3_out_4_fdb79afc));
  decoder_2_bit decoder_2_bit_4 (
    .in_1_2c4f912e(read_3), .in_2_2398e526(read_4), .out_1_367624e9(decoder_2_bit_4_out_1_367624e9),
    .out_2_0610cceb(decoder_2_bit_4_out_2_0610cceb), .out_3_f383ddb4(decoder_2_bit_4_out_3_f383ddb4),
    .out_4_fdb79afc(decoder_2_bit_4_out_4_fdb79afc));
  LED led_1 (.in(enable_read));
  LED led_2 (.in(enable_write));
  LED led_3 (.in(input_value));
  and and_1 (and_1_out, decoder_2_bit_2_out_1_367624e9, enable_write);
  and and_2 (and_2_out, decoder_2_bit_4_out_1_367624e9, enable_read);
  and and_3 (and_3_out, decoder_2_bit_2_out_2_0610cceb, enable_write);
  and and_4 (and_4_out, decoder_2_bit_4_out_2_0610cceb, enable_read);
  and and_5 (and_5_out, decoder_2_bit_2_out_3_f383ddb4, enable_write);
  and and_6 (and_6_out, decoder_2_bit_4_out_3_f383ddb4, enable_read);
  and and_7 (and_7_out, decoder_2_bit_2_out_4_fdb79afc, enable_write);
  and and_8 (and_8_out, decoder_2_bit_4_out_4_fdb79afc, enable_read);
  and and_9 (and_9_out, enable_read, decoder_2_bit_3_out_4_fdb79afc);
  or or_1 (or_1_out, and_1_out, and_2_out);
  or or_2 (or_2_out, and_3_out, and_4_out);
  or or_3 (or_3_out, and_5_out, and_6_out);
  or or_4 (or_4_out, and_7_out, and_8_out);
  and and_10 (and_10_out, enable_write, decoder_2_bit_1_out_4_fdb79afc);
  or or_5 (or_5_out, and_9_out, and_10_out);
  and and_11 (and_11_out, or_5_out, or_1_out);
  LED led_4 (.in(and_11_out));
  and and_12 (and_12_out, and_11_out, enable_read);
  and and_13 (and_13_out, and_11_out, enable_write);
  and and_14 (and_14_out, or_5_out, or_2_out);
  LED led_5 (.in(and_14_out));
  and and_15 (and_15_out, and_14_out, enable_read);
  and and_16 (and_16_out, and_14_out, enable_write);
  and and_17 (and_17_out, or_5_out, or_3_out);
  LED led_6 (.in(and_17_out));
  and and_18 (and_18_out, and_17_out, enable_read);
  and and_19 (and_19_out, and_17_out, enable_write);
  and and_20 (and_20_out, or_5_out, or_4_out);
  LED led_7 (.in(and_20_out));
  and and_21 (and_21_out, and_20_out, enable_read);
  and and_22 (and_22_out, and_20_out, enable_write);
  and and_23 (and_23_out, and_12_out, gated_latch_1_out_3);
  LED led_8 (.in(gated_latch_1_out_3));
  Gated_Latch gated_latch_1 (.set(input_value), .reset(and_13_out), .out_3(gated_latch_1_out_3));
  or or_6 (or_6_out, and_24_out, and_23_out);
  and and_24 (and_24_out, and_15_out, gated_latch_2_out_3);
  LED led_9 (.in(gated_latch_2_out_3));
  Gated_Latch gated_latch_2 (.set(input_value), .reset(and_16_out), .out_3(gated_latch_2_out_3));
  or or_7 (or_7_out, and_25_out, or_6_out);
  and and_25 (and_25_out, and_18_out, gated_latch_3_out_3);
  LED led_10 (.in(gated_latch_3_out_3));
  Gated_Latch gated_latch_3 (.set(input_value), .reset(and_19_out), .out_3(gated_latch_3_out_3));
  or or_8 (or_8_out, and_26_out, or_7_out);
  and and_26 (and_26_out, and_21_out, gated_latch_4_out_3);
  LED led_11 (.in(gated_latch_4_out_3));
  Gated_Latch gated_latch_4 (.set(input_value), .reset(and_22_out), .out_3(gated_latch_4_out_3));
  and and_27 (and_27_out, enable_read, decoder_2_bit_3_out_3_f383ddb4);
  or or_9 (or_9_out, and_27_out, and_28_out);
  and and_28 (and_28_out, enable_write, decoder_2_bit_1_out_3_f383ddb4);
  and and_29 (and_29_out, or_9_out, or_1_out);
  LED led_12 (.in(and_29_out));
  and and_30 (and_30_out, and_29_out, enable_read);
  and and_31 (and_31_out, and_29_out, enable_write);
  Gated_Latch gated_latch_5 (.set(input_value), .reset(and_31_out), .out_3(gated_latch_5_out_3));
  and and_32 (and_32_out, or_9_out, or_2_out);
  LED led_13 (.in(and_32_out));
  and and_33 (and_33_out, and_32_out, enable_read);
  and and_34 (and_34_out, and_32_out, enable_write);
  Gated_Latch gated_latch_6 (.set(input_value), .reset(and_34_out), .out_3(gated_latch_6_out_3));
  and and_35 (and_35_out, or_9_out, or_3_out);
  LED led_14 (.in(and_35_out));
  and and_36 (and_36_out, and_35_out, enable_read);
  and and_37 (and_37_out, and_35_out, enable_write);
  Gated_Latch gated_latch_7 (.set(input_value), .reset(and_37_out), .out_3(gated_latch_7_out_3));
  and and_38 (and_38_out, or_9_out, or_4_out);
  LED led_15 (.in(and_38_out));
  and and_39 (and_39_out, and_38_out, enable_read);
  and and_40 (and_40_out, and_38_out, enable_write);
  Gated_Latch gated_latch_8 (.set(input_value), .reset(and_40_out), .out_3(gated_latch_8_out_3));
  and and_41 (and_41_out, enable_read, decoder_2_bit_3_out_2_0610cceb);
  and and_42 (and_42_out, and_30_out, gated_latch_5_out_3);
  LED led_16 (.in(gated_latch_5_out_3));
  or or_10 (or_10_out, and_43_out, and_42_out);
  and and_43 (and_43_out, and_33_out, gated_latch_6_out_3);
  LED led_17 (.in(gated_latch_6_out_3));
  or or_11 (or_11_out, and_44_out, or_10_out);
  and and_44 (and_44_out, and_36_out, gated_latch_7_out_3);
  LED led_18 (.in(gated_latch_7_out_3));
  or or_12 (or_12_out, and_45_out, or_11_out);
  and and_45 (and_45_out, and_39_out, gated_latch_8_out_3);
  LED led_19 (.in(gated_latch_8_out_3));
  and and_46 (and_46_out, enable_write, decoder_2_bit_1_out_2_0610cceb);
  or or_13 (or_13_out, and_41_out, and_46_out);
  or or_14 (or_14_out, or_12_out, or_8_out);
  and and_47 (and_47_out, or_13_out, or_1_out);
  LED led_20 (.in(and_47_out));
  and and_48 (and_48_out, and_47_out, enable_read);
  and and_49 (and_49_out, and_47_out, enable_write);
  and and_50 (and_50_out, or_13_out, or_2_out);
  LED led_21 (.in(and_50_out));
  and and_51 (and_51_out, and_50_out, enable_read);
  and and_52 (and_52_out, and_50_out, enable_write);
  and and_53 (and_53_out, or_13_out, or_3_out);
  LED led_22 (.in(and_53_out));
  and and_54 (and_54_out, and_53_out, enable_read);
  and and_55 (and_55_out, and_53_out, enable_write);
  and and_56 (and_56_out, or_13_out, or_4_out);
  LED led_23 (.in(and_56_out));
  and and_57 (and_57_out, and_56_out, enable_read);
  and and_58 (and_58_out, and_56_out, enable_write);
  and and_59 (and_59_out, and_48_out, gated_latch_9_out_3);
  LED led_24 (.in(gated_latch_9_out_3));
  Gated_Latch gated_latch_9 (.set(input_value), .reset(and_49_out), .out_3(gated_latch_9_out_3));
  and and_60 (and_60_out, and_51_out, gated_latch_10_out_3);
  LED led_25 (.in(gated_latch_10_out_3));
  Gated_Latch gated_latch_10 (.set(input_value), .reset(and_52_out), .out_3(gated_latch_10_out_3));
  and and_61 (and_61_out, and_54_out, gated_latch_11_out_3);
  LED led_26 (.in(gated_latch_11_out_3));
  Gated_Latch gated_latch_11 (.set(input_value), .reset(and_55_out), .out_3(gated_latch_11_out_3));
  and and_62 (and_62_out, and_57_out, gated_latch_12_out_3);
  LED led_27 (.in(gated_latch_12_out_3));
  Gated_Latch gated_latch_12 (.set(input_value), .reset(and_58_out), .out_3(gated_latch_12_out_3));
  and and_63 (and_63_out, enable_read, decoder_2_bit_3_out_1_367624e9);
  or or_15 (or_15_out, and_63_out, and_64_out);
  or or_16 (or_16_out, and_60_out, and_59_out);
  or or_17 (or_17_out, and_61_out, or_16_out);
  or or_18 (or_18_out, and_62_out, or_17_out);
  or or_19 (or_19_out, or_18_out, or_14_out);
  and and_64 (and_64_out, enable_write, decoder_2_bit_1_out_1_367624e9);
  and and_65 (and_65_out, or_15_out, or_1_out);
  LED led_28 (.in(and_65_out));
  and and_66 (and_66_out, and_65_out, enable_read);
  and and_67 (and_67_out, and_65_out, enable_write);
  and and_68 (and_68_out, or_15_out, or_2_out);
  LED led_29 (.in(and_68_out));
  and and_69 (and_69_out, and_68_out, enable_read);
  and and_70 (and_70_out, and_68_out, enable_write);
  and and_71 (and_71_out, or_15_out, or_3_out);
  LED led_30 (.in(and_71_out));
  and and_72 (and_72_out, and_71_out, enable_read);
  and and_73 (and_73_out, and_71_out, enable_write);
  and and_74 (and_74_out, or_15_out, or_4_out);
  LED led_31 (.in(and_74_out));
  and and_75 (and_75_out, and_74_out, enable_read);
  and and_76 (and_76_out, and_74_out, enable_write);
  and and_77 (and_77_out, and_66_out, gated_latch_13_out_3);
  LED led_32 (.in(gated_latch_13_out_3));
  Gated_Latch gated_latch_13 (.set(input_value), .reset(and_67_out), .out_3(gated_latch_13_out_3));
  or or_20 (or_20_out, and_78_out, and_77_out);
  and and_78 (and_78_out, and_69_out, gated_latch_14_out_3);
  LED led_33 (.in(gated_latch_14_out_3));
  Gated_Latch gated_latch_14 (.set(input_value), .reset(and_70_out), .out_3(gated_latch_14_out_3));
  or or_21 (or_21_out, and_79_out, or_20_out);
  and and_79 (and_79_out, and_72_out, gated_latch_15_out_3);
  LED led_34 (.in(gated_latch_15_out_3));
  Gated_Latch gated_latch_15 (.set(input_value), .reset(and_73_out), .out_3(gated_latch_15_out_3));
  or or_22 (or_22_out, and_80_out, or_21_out);
  and and_80 (and_80_out, and_75_out, gated_latch_16_out_3);
  LED led_35 (.in(gated_latch_16_out_3));
  Gated_Latch gated_latch_16 (.set(input_value), .reset(and_76_out), .out_3(gated_latch_16_out_3));
  or or_23 (output_value, or_22_out, or_19_out);
  LED led_36 (.in(output_value));
endmodule

module adress_memory_16_x_1_byte (
  input  bit_1_1,
  input  bit_2_2,
  input  bit_3_4,
  input  bit_4_8,
  input  bit_5_16,
  input  bit_6_32,
  input  bit_7_64,
  input  bit_8_128,
  input  a_1,
  input  a_2,
  input  a_3,
  input  a_4,
  input  enable_read,
  input  enable_write,
  output out_1_1,
  output out_2_2,
  output out_3_4,
  output out_4_8,
  output out_5_16,
  output out_6_32,
  output out_7_64,
  output out_8_128
);

  adress_memory_16_bit adress_memory_16_bit_1 (
    .write_1(a_1), .write_2(a_2), .write_3(a_3), .write_4(a_4), .read_1(enable_read), .read_2(enable_write),
    .read_3(bit_1_1), .enable_write(a_1), .input_value(a_2), .output_value(out_8_128));  // open: read_4, enable_read
  adress_memory_16_bit adress_memory_16_bit_2 (
    .write_1(a_1), .write_2(a_2), .write_3(a_3), .write_4(a_4), .read_1(enable_read), .read_2(enable_write),
    .read_3(bit_2_2), .enable_write(a_1), .input_value(a_2), .output_value(out_7_64));  // open: read_4, enable_read
  adress_memory_16_bit adress_memory_16_bit_3 (
    .write_1(a_1), .write_2(a_2), .write_3(a_3), .write_4(a_4), .read_1(enable_read), .read_2(enable_write),
    .read_3(bit_3_4), .enable_write(a_1), .input_value(a_2), .output_value(out_6_32));  // open: read_4, enable_read
  adress_memory_16_bit adress_memory_16_bit_4 (
    .write_1(a_1), .write_2(a_2), .write_3(a_3), .write_4(a_4), .read_1(enable_read), .read_2(enable_write),
    .read_3(bit_4_8), .enable_write(a_1), .input_value(a_2), .output_value(out_5_16));  // open: read_4, enable_read
  adress_memory_16_bit adress_memory_16_bit_5 (
    .write_1(a_1), .write_2(a_2), .write_3(a_3), .write_4(a_4), .read_1(enable_read), .read_2(enable_write),
    .read_3(bit_5_16), .enable_write(a_1), .input_value(a_2), .output_value(out_4_8));  // open: read_4, enable_read
  adress_memory_16_bit adress_memory_16_bit_6 (
    .write_1(a_1), .write_2(a_2), .write_3(a_3), .write_4(a_4), .read_1(enable_read), .read_2(enable_write),
    .read_3(bit_6_32), .enable_write(a_1), .input_value(a_2), .output_value(out_3_4));  // open: read_4, enable_read
  adress_memory_16_bit adress_memory_16_bit_7 (
    .write_1(a_1), .write_2(a_2), .write_3(a_3), .write_4(a_4), .read_1(enable_read), .read_2(enable_write),
    .read_3(bit_7_64), .enable_write(a_1), .input_value(a_2), .output_value(out_2_2));  // open: read_4, enable_read
  adress_memory_16_bit adress_memory_16_bit_8 (
    .write_1(a_1), .write_2(a_2), .write_3(a_3), .write_4(a_4), .read_1(enable_read), .read_2(enable_write),
    .read_3(bit_8_128), .output_value(out_1_1));  // open: read_4, enable_read, enable_write, input_value

  // Notes on the sheet:
  //   Data_Bus
  //   Adress_Bus
endmodule

module memory_cell_1_bit (
  input  data_in,
  input  enable_write,
  output data_out
);

  wire and_1_out, and_2_out, not_1_out, not_2_out, or_1_out;

  not not_1 (not_1_out, data_in);
  and and_1 (and_1_out, data_in, enable_write);
  and and_2 (and_2_out, not_1_out, enable_write);
  not not_2 (not_2_out, and_2_out);
  or or_1 (or_1_out, data_out, and_1_out);
  and and_3 (data_out, or_1_out, not_2_out);
endmodule

module adress_memory_write_tp_self (
  input  write_adress_1,
  input  write_adress_2,
  input  write_adress_3,
  input  write_adress_4,
  input  read_adress_1,
  input  read_adress_2,
  input  read_adress_3,
  input  read_adress_4,
  input  enable_read,
  input  enable_write,
  input  switch_input,
  input  data_in_1,
  input  data_in_2,
  input  data_in_3,
  input  data_in_4,
  input  data_in_5,
  input  data_in_6,
  input  data_in_7,
  input  data_in_8,
  output out_20,
  output out_21,
  output out_22,
  output out_23,
  output out_24,
  output out_25,
  output out_26,
  output out_27
);

  wire mux_1_out_4, mux_2_out_4, mux_3_out_4, mux_4_out_4, mux_5_out_4, mux_6_out_4, mux_7_out_4, mux_8_out_4;

  MUX mux_1 (.in_2(out_20), .in_3(data_in_1), .in_1(switch_input), .out_4(mux_1_out_4));
  MUX mux_2 (.in_2(out_21), .in_3(data_in_2), .in_1(switch_input), .out_4(mux_2_out_4));
  MUX mux_3 (.in_2(out_22), .in_3(data_in_3), .in_1(switch_input), .out_4(mux_3_out_4));
  MUX mux_4 (.in_2(out_23), .in_3(data_in_4), .in_1(switch_input), .out_4(mux_4_out_4));
  MUX mux_5 (.in_2(out_24), .in_3(data_in_5), .in_1(switch_input), .out_4(mux_5_out_4));
  MUX mux_6 (.in_2(out_25), .in_3(data_in_6), .in_1(switch_input), .out_4(mux_6_out_4));
  MUX mux_7 (.in_2(out_26), .in_3(data_in_7), .in_1(switch_input), .out_4(mux_7_out_4));
  MUX mux_8 (.in_2(out_27), .in_3(data_in_8), .in_1(switch_input), .out_4(mux_8_out_4));
  adress_memory_16_bit adress_memory_16_bit_1 (
    .write_1(write_adress_1), .write_2(write_adress_2), .write_3(write_adress_3), .write_4(write_adress_4),
    .read_1(read_adress_1), .read_2(read_adress_2), .read_3(read_adress_3), .read_4(read_adress_4),
    .enable_read(enable_read), .enable_write(enable_write), .input_value(mux_1_out_4), .output_value(out_20));
  adress_memory_16_bit adress_memory_16_bit_2 (
    .write_1(write_adress_1), .write_2(write_adress_2), .write_3(write_adress_3), .write_4(write_adress_4),
    .read_1(read_adress_1), .read_2(read_adress_2), .read_3(read_adress_3), .read_4(read_adress_4),
    .enable_read(enable_read), .enable_write(enable_write), .input_value(mux_2_out_4), .output_value(out_21));
  adress_memory_16_bit adress_memory_16_bit_3 (
    .write_1(write_adress_1), .write_2(write_adress_2), .write_3(write_adress_3), .write_4(write_adress_4),
    .read_1(read_adress_1), .read_2(read_adress_2), .read_3(read_adress_3), .read_4(read_adress_4),
    .enable_read(enable_read), .enable_write(enable_write), .input_value(mux_3_out_4), .output_value(out_22));
  adress_memory_16_bit adress_memory_16_bit_4 (
    .write_1(write_adress_1), .write_2(write_adress_2), .write_3(write_adress_3), .write_4(write_adress_4),
    .read_1(read_adress_1), .read_2(read_adress_2), .read_3(read_adress_3), .read_4(read_adress_4),
    .enable_read(enable_read), .enable_write(enable_write), .input_value(mux_4_out_4), .output_value(out_23));
  adress_memory_16_bit adress_memory_16_bit_5 (
    .write_1(write_adress_1), .write_2(write_adress_2), .write_3(write_adress_3), .write_4(write_adress_4),
    .read_1(read_adress_1), .read_2(read_adress_2), .read_3(read_adress_3), .read_4(read_adress_4),
    .enable_read(enable_read), .enable_write(enable_write), .input_value(mux_5_out_4), .output_value(out_24));
  adress_memory_16_bit adress_memory_16_bit_6 (
    .write_1(write_adress_1), .write_2(write_adress_2), .write_3(write_adress_3), .write_4(write_adress_4),
    .read_1(read_adress_1), .read_2(read_adress_2), .read_3(read_adress_3), .read_4(read_adress_4),
    .enable_read(enable_read), .enable_write(enable_write), .input_value(mux_6_out_4), .output_value(out_25));
  adress_memory_16_bit adress_memory_16_bit_7 (
    .write_1(write_adress_1), .write_2(write_adress_2), .write_3(write_adress_3), .write_4(write_adress_4),
    .read_1(read_adress_1), .read_2(read_adress_2), .read_3(read_adress_3), .read_4(read_adress_4),
    .enable_read(enable_read), .enable_write(enable_write), .input_value(mux_7_out_4), .output_value(out_26));
  adress_memory_16_bit adress_memory_16_bit_8 (
    .write_1(write_adress_1), .write_2(write_adress_2), .write_3(write_adress_3), .write_4(write_adress_4),
    .read_1(read_adress_1), .read_2(read_adress_2), .read_3(read_adress_3), .read_4(read_adress_4),
    .enable_read(enable_read), .enable_write(enable_write), .input_value(mux_8_out_4), .output_value(out_27));
endmodule

module MUX (
  input  in_1,
  input  in_2,
  input  in_3,
  output out_4
);

  wire and_1_out, and_2_out, not_1_out;

  not not_1 (not_1_out, in_1);
  and and_1 (and_1_out, not_1_out, in_2);
  and and_2 (and_2_out, in_1, in_3);
  or or_1 (out_4, and_1_out, and_2_out);
endmodule

module Byte_MUX (
  input  select_input,
  input  [7:0] in_0,
  input  [7:0] in_1,
  output [7:0] out_4
);

  MUX mux_1 (.in_2(in_0[0]), .in_3(in_1[0]), .in_1(select_input), .out_4(out_4[0]));
  MUX mux_2 (.in_2(in_0[1]), .in_3(in_1[1]), .in_1(select_input), .out_4(out_4[1]));
  MUX mux_3 (.in_2(in_0[2]), .in_3(in_1[2]), .in_1(select_input), .out_4(out_4[2]));
  MUX mux_4 (.in_2(in_0[3]), .in_3(in_1[3]), .in_1(select_input), .out_4(out_4[3]));
  MUX mux_5 (.in_2(in_0[4]), .in_3(in_1[4]), .in_1(select_input), .out_4(out_4[4]));
  MUX mux_6 (.in_2(in_0[5]), .in_3(in_1[5]), .in_1(select_input), .out_4(out_4[5]));
  MUX mux_7 (.in_2(in_0[6]), .in_3(in_1[6]), .in_1(select_input), .out_4(out_4[6]));
  MUX mux_8 (.in_2(in_0[7]), .in_3(in_1[7]), .in_1(select_input), .out_4(out_4[7]));
endmodule

module Byter_adder (
  input  [7:0] i_1,
  input  [7:0] i_2,
  output [7:0] o_1,
  output carry
);

  wire full_adder_1_count, full_adder_2_count, full_adder_3_count, full_adder_4_count, full_adder_5_count,
       full_adder_6_count, full_adder_7_count;

  full_adder full_adder_1 (.A(i_2[0]), .B(i_1[0]), .sum(o_1[0]), .count(full_adder_1_count));  // open: C_in_6a097d25
  full_adder full_adder_2 (
    .A(full_adder_1_count), .B(i_1[1]), .C_in_6a097d25(i_2[1]), .sum(o_1[1]), .count(full_adder_2_count));
  full_adder full_adder_3 (
    .A(full_adder_2_count), .B(i_1[2]), .C_in_6a097d25(i_2[2]), .sum(o_1[2]), .count(full_adder_3_count));
  full_adder full_adder_4 (
    .A(full_adder_3_count), .B(i_1[3]), .C_in_6a097d25(i_2[3]), .sum(o_1[3]), .count(full_adder_4_count));
  full_adder full_adder_5 (
    .A(full_adder_4_count), .B(i_1[4]), .C_in_6a097d25(i_2[4]), .sum(o_1[4]), .count(full_adder_5_count));
  full_adder full_adder_6 (
    .A(full_adder_5_count), .B(i_1[5]), .C_in_6a097d25(i_2[5]), .sum(o_1[5]), .count(full_adder_6_count));
  full_adder full_adder_7 (
    .A(full_adder_6_count), .B(i_1[6]), .C_in_6a097d25(i_2[6]), .sum(o_1[6]), .count(full_adder_7_count));
  full_adder full_adder_8 (.A(full_adder_7_count), .B(i_1[7]), .C_in_6a097d25(i_2[7]), .sum(o_1[7]), .count(carry));
endmodule

module Byte_inverter (
  input  [7:0] in_1,
  output [7:0] out_2
);

  not not_1 (out_2[0], in_1[0]);
  not not_2 (out_2[1], in_1[1]);
  not not_3 (out_2[2], in_1[2]);
  not not_4 (out_2[3], in_1[3]);
  not not_5 (out_2[4], in_1[4]);
  not not_6 (out_2[5], in_1[5]);
  not not_7 (out_2[6], in_1[6]);
  not not_8 (out_2[7], in_1[7]);
endmodule

module Byte_switch (
  input  switch,
  input  [7:0] i,
  output [7:0] o
);

  and and_1 (o[0], i[0], switch);
  and and_2 (o[1], i[1], switch);
  and and_3 (o[2], i[2], switch);
  and and_4 (o[3], i[3], switch);
  and and_5 (o[4], i[4], switch);
  and and_6 (o[5], i[5], switch);
  and and_7 (o[6], i[6], switch);
  and and_8 (o[7], i[7], switch);
endmodule

module MUX_4_Byte (
  input  [7:0] in_1,
  input  [7:0] b_0,
  input  [7:0] b_1,
  input  [7:0] b_2,
  input  [7:0] b_3,
  output [7:0] out_6
);

  wire or_1_out;
  wire [7:0] byte_mux_1_out_4, byte_mux_2_out_4, byte_switch_1_o, byte_switch_2_o, byte_switch_3_o,
       byte_switch_4_o;

  Byte_switch byte_switch_1 (.i(b_0), .switch(in_1[4]), .o(byte_switch_1_o));
  Byte_switch byte_switch_2 (.i(b_1), .switch(in_1[5]), .o(byte_switch_2_o));
  Byte_switch byte_switch_3 (.i(b_2), .switch(in_1[6]), .o(byte_switch_3_o));
  Byte_switch byte_switch_4 (.i(b_3), .switch(in_1[7]), .o(byte_switch_4_o));
  or or_1 (or_1_out, in_1[6], in_1[7]);
  Byte_MUX byte_mux_1 (
    .select_input(in_1[5]), .in_0(byte_switch_1_o), .in_1(byte_switch_2_o), .out_4(byte_mux_1_out_4));
  Byte_MUX byte_mux_2 (
    .select_input(in_1[7]), .in_0(byte_switch_3_o), .in_1(byte_switch_4_o), .out_4(byte_mux_2_out_4));
  Byte_MUX byte_mux_3 (.select_input(or_1_out), .in_0(byte_mux_1_out_4), .in_1(byte_mux_2_out_4), .out_4(out_6));
endmodule

module Byte_decoder (
  input  [7:0] adress_bus_in,
  output adress_0,
  output adress_1,
  output adress_2,
  output adress_3
);

  wire and_1_out, and_2_out, and_3_out, and_4_out, nor_1_out, not_1_out, not_2_out, not_3_out, not_4_out,
       not_5_out, not_6_out, not_7_out, not_8_out, not_9_out;

  not not_1 (not_1_out, adress_bus_in[1]);
  not not_2 (not_2_out, adress_bus_in[2]);
  not not_3 (not_3_out, adress_bus_in[3]);
  not not_4 (not_4_out, adress_bus_in[0]);
  not not_5 (not_5_out, adress_bus_in[3]);
  not not_6 (not_6_out, adress_bus_in[2]);
  nor nor_1 (nor_1_out, adress_bus_in[3], adress_bus_in[2]);
  not not_7 (not_7_out, adress_bus_in[0]);
  not not_8 (not_8_out, adress_bus_in[1]);
  not not_9 (not_9_out, adress_bus_in[3]);
  and and_1 (and_1_out, adress_bus_in[0], not_1_out, not_2_out, not_3_out);
  and and_2 (and_2_out, not_4_out, adress_bus_in[1], not_5_out, not_6_out);
  and and_3 (and_3_out, nor_1_out, adress_bus_in[1], adress_bus_in[0]);
  and and_4 (and_4_out, adress_bus_in[2], not_7_out, not_8_out, not_9_out);
  and and_5 (adress_0, and_1_out, adress_bus_in[7]);
  and and_6 (adress_1, and_2_out, adress_bus_in[7]);
  and and_7 (adress_2, and_3_out, adress_bus_in[7]);
  and and_8 (adress_3, and_4_out, adress_bus_in[7]);
endmodule

module Adress_dcoder (
  input  [7:0] in_1,
  output adress_0,
  output adress_1,
  output adress_2,
  output adress_3
);

  wire nor_1_out, not_1_out, not_2_out, not_3_out, not_4_out, not_5_out, not_6_out;

  not not_1 (not_1_out, in_1[5]);
  not not_2 (not_2_out, in_1[6]);
  not not_3 (not_3_out, in_1[4]);
  not not_4 (not_4_out, in_1[6]);
  not nor_1 (nor_1_out, in_1[6]);  // NOR_Gate
  not not_5 (not_5_out, in_1[4]);
  not not_6 (not_6_out, in_1[5]);
  and and_1 (adress_0, in_1[4], not_1_out, not_2_out);
  and and_2 (adress_1, not_3_out, in_1[5], not_4_out);
  and and_3 (adress_2, nor_1_out, in_1[5], in_1[4]);
  and and_4 (adress_3, in_1[6], not_5_out, not_6_out);
endmodule

module read_to_self (
  input  [7:0] in_1
);
endmodule

module tmp (
  input  [7:0] adress_bus_in,
  output adress_0,
  output adress_1,
  output adress_2,
  output adress_3
);

  wire nor_1_out, not_1_out, not_2_out, not_3_out, not_4_out, not_5_out, not_6_out, not_7_out, not_8_out,
       not_9_out;

  not not_1 (not_1_out, adress_bus_in[1]);
  not not_2 (not_2_out, adress_bus_in[2]);
  not not_3 (not_3_out, adress_bus_in[3]);
  not not_4 (not_4_out, adress_bus_in[0]);
  not not_5 (not_5_out, adress_bus_in[3]);
  not not_6 (not_6_out, adress_bus_in[2]);
  nor nor_1 (nor_1_out, adress_bus_in[3], adress_bus_in[2]);
  not not_7 (not_7_out, adress_bus_in[0]);
  not not_8 (not_8_out, adress_bus_in[1]);
  not not_9 (not_9_out, adress_bus_in[3]);
  and and_1 (adress_0, adress_bus_in[0], not_1_out, not_2_out, not_3_out);
  and and_2 (adress_1, not_4_out, adress_bus_in[1], not_5_out, not_6_out);
  and and_3 (adress_2, nor_1_out, adress_bus_in[1], adress_bus_in[0]);
  and and_4 (adress_3, adress_bus_in[2], not_7_out, not_8_out, not_9_out);
endmodule

module Instruction_decoder (
  input  [7:0] in_1,
  output read_reg,
  output read_bus
);

  wire nor_1_out, nor_2_out;

  nor nor_1 (nor_1_out, in_1[7], in_1[6], in_1[5], in_1[4], in_1[3], in_1[2], in_1[0]);
  and and_1 (read_reg, nor_1_out, in_1[1]);
  and and_2 (read_bus, in_1[0], nor_2_out);
  nor nor_2 (nor_2_out, in_1[1], in_1[2], in_1[3], in_1[4], in_1[5], in_1[6], in_1[7]);
endmodule

module temp (
  input  [7:0] in_1,
  output out_2
);

  wire nor_1_out;

  nor nor_1 (nor_1_out, in_1[2], in_1[3], in_1[4], in_1[5], in_1[6], in_1[7]);
  and and_1 (out_2, in_1[0], in_1[1], nor_1_out);
endmodule

module comperater (
  input  [7:0] instruction_bus,
  input  [7:0] data_in
);

  wire and_1_out, and_2_out, and_3_out, and_4_out, and_5_out, and_6_out, and_7_out, and_8_out, nor_1_out,
       nor_2_out, nor_3_out, nor_4_out, nor_5_out, nor_6_out, nor_7_out, or_1_out;

  nor nor_1 (nor_1_out, instruction_bus[0], instruction_bus[2], instruction_bus[4], instruction_bus[5], instruction_bus[6], instruction_bus[7]);
  nor nor_2 (nor_2_out, instruction_bus[2], instruction_bus[4], instruction_bus[5], instruction_bus[6], instruction_bus[7]);
  nor nor_3 (nor_3_out, instruction_bus[4], instruction_bus[5], instruction_bus[6], instruction_bus[7], instruction_bus[1], instruction_bus[0]);
  nor nor_4 (nor_4_out, instruction_bus[4], instruction_bus[5], instruction_bus[6], instruction_bus[7], instruction_bus[1]);
  nor nor_5 (nor_5_out, instruction_bus[4], instruction_bus[5], instruction_bus[6], instruction_bus[7], instruction_bus[0]);
  nor nor_6 (nor_6_out, instruction_bus[4], instruction_bus[5], instruction_bus[6], instruction_bus[7]);
  and and_1 (and_1_out, instruction_bus[1], instruction_bus[3], nor_1_out);
  and and_2 (and_2_out, instruction_bus[1], instruction_bus[3], instruction_bus[0], nor_2_out);
  and and_3 (and_3_out, instruction_bus[3], instruction_bus[2], nor_3_out);
  and and_4 (and_4_out, instruction_bus[3], instruction_bus[0], instruction_bus[2], nor_4_out);
  and and_5 (and_5_out, instruction_bus[3], instruction_bus[2], instruction_bus[1], nor_5_out);
  and and_6 (and_6_out, instruction_bus[3], instruction_bus[2], instruction_bus[1], instruction_bus[0], nor_6_out);
  nor nor_7 (nor_7_out, data_in[0], data_in[1], data_in[2], data_in[3], data_in[4], data_in[5], data_in[6], data_in[7]);
  and and_7 (and_7_out, and_1_out, nor_7_out);
  or or_1 (or_1_out, data_in[0], data_in[1], data_in[2], data_in[3], data_in[4], data_in[5], data_in[6], data_in[7]);
  and and_8 (and_8_out, and_2_out, or_1_out);
endmodule

module alu_decoder (
  input  [7:0] instruction_Bus_in,
  output subtraction,
  output addition,
  output equals_zweo,
  output not_zero,
  output greater_zero,
  output smaller_zero,
  output greater_equal_zero,
  output smaller_equal_zero
);

  wire nor_1_out, nor_2_out, nor_3_out, nor_4_out, nor_5_out, nor_6_out, nor_7_out, nor_8_out;

  nor nor_1 (nor_1_out, instruction_Bus_in[7], instruction_Bus_in[5], instruction_Bus_in[4], instruction_Bus_in[3]);
  nor nor_2 (nor_2_out, instruction_Bus_in[0], instruction_Bus_in[3], instruction_Bus_in[4], instruction_Bus_in[5], instruction_Bus_in[7]);
  nor nor_3 (nor_3_out, instruction_Bus_in[0], instruction_Bus_in[2], instruction_Bus_in[4], instruction_Bus_in[5], instruction_Bus_in[7]);
  nor nor_4 (nor_4_out, instruction_Bus_in[2], instruction_Bus_in[4], instruction_Bus_in[5], instruction_Bus_in[7]);
  nor nor_5 (nor_5_out, instruction_Bus_in[4], instruction_Bus_in[5], instruction_Bus_in[7], instruction_Bus_in[1], instruction_Bus_in[0]);
  nor nor_6 (nor_6_out, instruction_Bus_in[4], instruction_Bus_in[5], instruction_Bus_in[7], instruction_Bus_in[1]);
  nor nor_7 (nor_7_out, instruction_Bus_in[4], instruction_Bus_in[5], instruction_Bus_in[7], instruction_Bus_in[0]);
  nor nor_8 (nor_8_out, instruction_Bus_in[4], instruction_Bus_in[5], instruction_Bus_in[7]);
  and and_1 (subtraction, nor_1_out, instruction_Bus_in[2], instruction_Bus_in[1], instruction_Bus_in[0]);
  and and_2 (addition, instruction_Bus_in[1], instruction_Bus_in[2], nor_2_out);
  and and_3 (equals_zweo, instruction_Bus_in[3], instruction_Bus_in[1], nor_3_out);
  and and_4 (not_zero, instruction_Bus_in[3], instruction_Bus_in[1], instruction_Bus_in[0], nor_4_out);
  and and_5 (greater_zero, instruction_Bus_in[3], instruction_Bus_in[2], nor_5_out);
  and and_6 (smaller_zero, instruction_Bus_in[3], instruction_Bus_in[2], instruction_Bus_in[0], nor_6_out);
  and and_7 (greater_equal_zero, instruction_Bus_in[3], instruction_Bus_in[2], instruction_Bus_in[1], nor_7_out);
  and and_8 (smaller_equal_zero, instruction_Bus_in[3], instruction_Bus_in[2], instruction_Bus_in[1], instruction_Bus_in[0], nor_8_out);
endmodule

module reg_to_bus (
  input  [7:0] bus_in,
  output o
);

  wire nor_1_out;

  nor nor_1 (nor_1_out, bus_in[2], bus_in[3], bus_in[4], bus_in[5], bus_in[6], bus_in[7]);
  and and_1 (o, bus_in[0], bus_in[1], nor_1_out);
endmodule

module comperator (
  input  [7:0] in_1
);
endmodule

module cpu_v3 (
  input  in_1,
  input  [7:0] in_2
);

  wire and_1_out, and_2_out, and_3_out, and_4_out, and_5_out, and_6_out, and_7_out, and_8_out, and_9_out,
       and_10_out, and_11_out, and_12_out, and_13_out, and_14_out, and_15_out, and_16_out, and_17_out,
       and_18_out, and_19_out, and_20_out, and_21_out, and_22_out, and_23_out, and_24_out, and_25_out,
       and_26_out, and_27_out, and_28_out, and_29_out, and_30_out, and_31_out, and_32_out, and_33_out,
       and_34_out, and_35_out, and_36_out, and_37_out, and_38_out, and_39_out, and_40_out, and_41_out,
       and_42_out, and_43_out, and_52_out, and_53_out, and_54_out, and_56_out, and_57_out, and_58_out,
       and_59_out, and_60_out, and_61_out, and_62_out, and_63_out, and_64_out, and_65_out, and_66_out,
       and_67_out, and_68_out, and_70_out, and_71_out, and_72_out, and_73_out, and_74_out, and_75_out,
       and_76_out, and_77_out, clock_1_out, equals_0_out, greater_0_out, greater_eaqual_out, left_out,
       nor_1_out, nor_2_out, nor_3_out, nor_4_out, nor_5_out, nor_6_out, nor_7_out, nor_8_out, nor_9_out,
       nor_10_out, nor_11_out, nor_12_out, nor_13_out, not_1_out, not_2_out, not_3_out, not_4_out, not_5_out,
       not_6_out, not_7_out, not_9_out, not_10_out, not_11_out, not_20_out, not_21_out, not_22_out,
       not_zero_out, or_1_out, or_2_out, or_3_out, or_4_out, or_5_out, or_6_out, or_7_out, or_8_out,
       or_9_out, or_10_out, or_11_out, or_12_out, or_13_out, or_20_out, or_21_out, or_22_out, right_out,
       smaller_equal_out, xor_1_out, xor_2_out, xor_3_out, xor_4_out, xor_5_out, xor_6_out, xor_7_out,
       xor_8_out, xor_9_out, xor_10_out, xor_11_out, xor_12_out, xor_13_out, xor_14_out, xor_15_out,
       xor_16_out;
  wire [3:0] byte_to_hex_display_1_out_2, byte_to_hex_display_1_out_3, byte_to_hex_display_2_out_2,
       byte_to_hex_display_2_out_3, byte_to_hex_display_3_out_2, byte_to_hex_display_3_out_3;
  wire [7:0] and_44_out, and_55_out, and_78_out, byte_mux_1_out_4, byte_mux_2_out_4, byte_mux_3_out_4,
       byte_mux_4_out_4, byte_mux_5_out_4, byte_or_1_out_3, byte_or_2_out_3, byte_or_3_out_3,
       byte_or_4_out_3, byte_or_5_out_3, byte_or_6_out_3, byte_or_7_out_3, byte_switch_1_o, byte_switch_2_o,
       byte_switch_3_o, byte_switch_4_o, byte_switch_5_o, byte_switch_6_o, byte_switch_7_o, byte_switch_8_o,
       counter_1_q, nand_1_out, nor_14_out, not_19_out, or_23_out, Reg_0_q, Reg_1_q, Reg_2_q, Reg_3_q,
       Reg_4_q, Reg_5_q, Reg_6_q, Reg_7_q, rom_1_data;
  wire [7:7] not_8_out;

  ROM rom_1 (.addr(counter_1_q), .data(rom_1_data));
  Counter counter_1 (
    .load(and_5_out), .D(Reg_7_q), .count(not_3_out), .Q(counter_1_q), .clk(clock_1_out));  // open: carry, up, clr
  LedBar ledbar_1 (
    .led0(rom_1_data[7]), .led1(rom_1_data[6]), .led2(rom_1_data[5]), .led3(rom_1_data[4]),
    .led4(rom_1_data[3]), .led5(rom_1_data[2]), .led6(rom_1_data[1]), .led7(rom_1_data[0]));
  Byte_MUX byte_mux_1 (.select_input(in_1), .in_0(rom_1_data), .in_1(in_2), .out_4(byte_mux_1_out_4));
  Byte_to_Hex_display byte_to_hex_display_1 (
    .in_1(in_2), .out_2(byte_to_hex_display_1_out_2), .out_3(byte_to_hex_display_1_out_3));
  Byte_to_Hex_display byte_to_hex_display_2 (
    .in_1(rom_1_data), .out_2(byte_to_hex_display_2_out_2), .out_3(byte_to_hex_display_2_out_3));
  not not_1 (not_1_out, byte_mux_1_out_4[6]);
  not not_2 (not_2_out, byte_mux_1_out_4[7]);
  Hex_Digit_Display hex_digit_display_1 (.value(byte_to_hex_display_1_out_3));  // open: dp
  Hex_Digit_Display hex_digit_display_2 (.value(byte_to_hex_display_2_out_3));  // open: dp
  and and_1 (and_1_out, byte_mux_1_out_4[6], byte_mux_1_out_4[7]);
  and and_2 (and_2_out, not_1_out, byte_mux_1_out_4[7]);
  and and_3 (and_3_out, byte_mux_1_out_4[6], not_2_out);
  nor nor_1 (nor_1_out, byte_mux_1_out_4[6], byte_mux_1_out_4[7]);
  Hex_Digit_Display hex_digit_display_3 (.value(byte_to_hex_display_1_out_2));  // open: dp
  Hex_Digit_Display hex_digit_display_4 (.value(byte_to_hex_display_2_out_2));  // open: dp
  Clock clock_1 (.out(clock_1_out));
  not not_3 (not_3_out, and_4_out);
  and and_4 (and_4_out, and_6_out, and_54_out);
  and and_5 (and_5_out, not_4_out, and_54_out);
  and and_6 (and_6_out, and_1_out, byte_mux_1_out_4[0]);
  and and_7 (and_7_out, or_1_out, byte_mux_1_out_4[2]);
  not not_4 (not_4_out, byte_mux_1_out_4[0]);
  and and_8 (and_8_out, or_1_out, byte_mux_1_out_4[1]);
  or or_1 (or_1_out, and_3_out, and_2_out);
  and and_9 (and_9_out, or_1_out, byte_mux_1_out_4[0]);
  nor nor_2 (nor_2_out, and_8_out, and_7_out);
  nor nor_3 (nor_3_out, and_7_out, and_9_out);
  not not_5 (not_5_out, and_7_out);
  nor nor_4 (nor_4_out, and_8_out, and_9_out);
  not not_6 (not_6_out, and_8_out);
  not not_7 (not_7_out, and_9_out);
  not not_8 (not_8_out[7], nor_1_out);
  nor nor_5 (nor_5_out, and_7_out, and_8_out, and_9_out);
  and and_10 (and_10_out, nor_2_out, and_9_out);
  and and_11 (and_11_out, nor_3_out, and_8_out);
  and and_12 (and_12_out, not_5_out, and_8_out, and_9_out);
  and and_13 (and_13_out, nor_4_out, and_7_out);
  and and_14 (and_14_out, and_7_out, not_6_out, and_9_out);
  and and_15 (and_15_out, and_7_out, and_8_out, not_7_out);
  and and_16 (and_16_out, and_7_out, and_8_out, and_9_out);
  Byte_MUX byte_mux_2 (
    .select_input(nor_1_out), .in_0(byte_mux_3_out_4), .in_1({{2{not_8_out[7]}}, byte_mux_1_out_4[5:0]}),
    .out_4(byte_mux_2_out_4));
  Register Reg_0 (.D(byte_mux_2_out_4), .en(nor_5_out), .clk(clock_1_out), .Q(Reg_0_q));  // open: clr
  Register Reg_1 (.D(byte_mux_2_out_4), .en(and_10_out), .clk(clock_1_out), .Q(Reg_1_q));  // open: clr
  Register Reg_2 (.D(byte_mux_2_out_4), .en(and_11_out), .clk(clock_1_out), .Q(Reg_2_q));  // open: clr
  Register Reg_3 (.D(byte_mux_2_out_4), .en(and_12_out), .clk(clock_1_out), .Q(Reg_3_q));  // open: clr
  Register Reg_4 (.D(byte_mux_2_out_4), .en(and_13_out), .clk(clock_1_out), .Q(Reg_4_q));  // open: clr
  Register Reg_5 (.D(byte_mux_2_out_4), .en(and_14_out), .clk(clock_1_out), .Q(Reg_5_q));  // open: clr
  Register Reg_6 (.D(byte_mux_2_out_4), .en(and_15_out), .clk(clock_1_out), .Q(Reg_6_q));  // open: clr
  Register Reg_7 (.D(byte_mux_2_out_4), .en(and_16_out), .clk(clock_1_out), .Q(Reg_7_q));  // open: clr
  Byte_switch byte_switch_1 (.i(Reg_0_q), .switch(nor_6_out), .o(byte_switch_1_o));
  Byte_switch byte_switch_2 (.i(Reg_1_q), .switch(and_17_out), .o(byte_switch_2_o));
  Byte_switch byte_switch_3 (.i(Reg_2_q), .switch(and_18_out), .o(byte_switch_3_o));
  Byte_switch byte_switch_4 (.i(Reg_3_q), .switch(and_19_out), .o(byte_switch_4_o));
  Byte_switch byte_switch_5 (.i(Reg_4_q), .switch(and_20_out), .o(byte_switch_5_o));
  Byte_switch byte_switch_6 (.i(Reg_5_q), .switch(and_21_out), .o(byte_switch_6_o));
  Byte_switch byte_switch_7 (.i(Reg_6_q), .switch(and_22_out), .o(byte_switch_7_o));
  Byte_switch byte_switch_8 (.i(Reg_7_q), .switch(and_23_out), .o(byte_switch_8_o));
  Byte_to_Hex_display byte_to_hex_display_3 (
    .in_1(byte_mux_3_out_4), .out_2(byte_to_hex_display_3_out_2), .out_3(byte_to_hex_display_3_out_3));
  Byte_MUX byte_mux_3 (
    .select_input(and_2_out), .in_0(byte_or_1_out_3), .in_1(byte_mux_5_out_4), .out_4(byte_mux_3_out_4));
  Byte_or byte_or_1 (.in_1(byte_switch_1_o), .in_2(byte_or_2_out_3), .out_3(byte_or_1_out_3));
  Byte_or byte_or_2 (.in_1(byte_switch_2_o), .in_2(byte_or_3_out_3), .out_3(byte_or_2_out_3));
  Byte_or byte_or_3 (.in_1(byte_switch_3_o), .in_2(byte_or_4_out_3), .out_3(byte_or_3_out_3));
  Byte_or byte_or_4 (.in_1(byte_switch_4_o), .in_2(byte_or_5_out_3), .out_3(byte_or_4_out_3));
  Byte_or byte_or_5 (.in_1(byte_switch_5_o), .in_2(byte_or_6_out_3), .out_3(byte_or_5_out_3));
  Byte_or byte_or_6 (.in_1(byte_switch_6_o), .in_2(byte_or_7_out_3), .out_3(byte_or_6_out_3));
  Byte_or byte_or_7 (.in_1(byte_switch_7_o), .in_2(byte_switch_8_o), .out_3(byte_or_7_out_3));
  Hex_Digit_Display hex_digit_display_5 (.value(byte_to_hex_display_3_out_3));  // open: dp
  Hex_Digit_Display hex_digit_display_6 (.value(byte_to_hex_display_3_out_2));  // open: dp
  nor nor_6 (nor_6_out, and_24_out, and_25_out, and_26_out);
  and and_17 (and_17_out, nor_7_out, and_26_out);
  and and_18 (and_18_out, nor_8_out, and_25_out);
  and and_19 (and_19_out, not_9_out, and_25_out, and_26_out);
  and and_20 (and_20_out, nor_9_out, and_24_out);
  and and_21 (and_21_out, and_24_out, not_10_out, and_26_out);
  and and_22 (and_22_out, and_24_out, and_25_out, not_11_out);
  and and_23 (and_23_out, and_24_out, and_25_out, and_26_out);
  and and_24 (and_24_out, and_3_out, byte_mux_1_out_4[5]);
  nor nor_7 (nor_7_out, and_24_out, and_25_out);
  nor nor_8 (nor_8_out, and_24_out, and_26_out);
  not not_9 (not_9_out, and_24_out);
  nor nor_9 (nor_9_out, and_25_out, and_26_out);
  not not_10 (not_10_out, and_25_out);
  not not_11 (not_11_out, and_26_out);
  and and_25 (and_25_out, and_3_out, byte_mux_1_out_4[4]);
  and and_26 (and_26_out, and_3_out, byte_mux_1_out_4[3]);
  Byte_MUX byte_mux_4 (.select_input(and_27_out), .in_0(Reg_2_q), .in_1(not_19_out), .out_4(byte_mux_4_out_4));
  not not_12 (not_19_out[7], Reg_2_q[7]);
  not not_13 (not_19_out[6], Reg_2_q[6]);
  not not_14 (not_19_out[5], Reg_2_q[5]);
  not not_15 (not_19_out[4], Reg_2_q[4]);
  not not_16 (not_19_out[3], Reg_2_q[3]);
  not not_17 (not_19_out[2], Reg_2_q[2]);
  not not_18 (not_19_out[1], Reg_2_q[1]);
  not not_19 (not_19_out[0], Reg_2_q[0]);
  and and_27 (and_27_out, and_2_out, byte_mux_1_out_4[5]);
  xor xor_1 (xor_1_out, byte_mux_4_out_4[0], Reg_1_q[0]);
  and and_28 (and_28_out, Reg_1_q[0], byte_mux_4_out_4[0]);
  xor xor_2 (xor_2_out, byte_mux_4_out_4[1], Reg_1_q[1]);
  and and_29 (and_29_out, Reg_1_q[1], byte_mux_4_out_4[1]);
  xor xor_3 (xor_3_out, byte_mux_4_out_4[2], Reg_1_q[2]);
  and and_30 (and_30_out, Reg_1_q[2], byte_mux_4_out_4[2]);
  xor xor_4 (xor_4_out, byte_mux_4_out_4[3], Reg_1_q[3]);
  and and_31 (and_31_out, Reg_1_q[3], byte_mux_4_out_4[3]);
  xor xor_5 (xor_5_out, byte_mux_4_out_4[4], Reg_1_q[4]);
  and and_32 (and_32_out, Reg_1_q[4], byte_mux_4_out_4[4]);
  xor xor_6 (xor_6_out, byte_mux_4_out_4[5], Reg_1_q[5]);
  and and_33 (and_33_out, Reg_1_q[5], byte_mux_4_out_4[5]);
  xor xor_7 (xor_7_out, byte_mux_4_out_4[6], Reg_1_q[6]);
  and and_34 (and_34_out, Reg_1_q[6], byte_mux_4_out_4[6]);
  xor xor_8 (xor_8_out, byte_mux_4_out_4[7], Reg_1_q[7]);
  and and_35 (and_35_out, Reg_1_q[7], byte_mux_4_out_4[7]);
  and and_36 (and_36_out, xor_1_out, and_27_out);
  and and_37 (and_37_out, xor_2_out, or_2_out);
  and and_38 (and_38_out, xor_3_out, or_3_out);
  and and_39 (and_39_out, xor_4_out, or_4_out);
  and and_40 (and_40_out, xor_5_out, or_5_out);
  and and_41 (and_41_out, xor_6_out, or_6_out);
  and and_42 (and_42_out, xor_7_out, or_7_out);
  and and_43 (and_43_out, xor_8_out, or_8_out);
  xor xor_9 (xor_9_out, xor_1_out, and_27_out);
  or or_2 (or_2_out, and_36_out, and_28_out);
  xor xor_10 (xor_10_out, xor_2_out, or_2_out);
  or or_3 (or_3_out, and_37_out, and_29_out);
  xor xor_11 (xor_11_out, xor_3_out, or_3_out);
  or or_4 (or_4_out, and_38_out, and_30_out);
  xor xor_12 (xor_12_out, xor_4_out, or_4_out);
  or or_5 (or_5_out, and_39_out, and_31_out);
  xor xor_13 (xor_13_out, xor_5_out, or_5_out);
  or or_6 (or_6_out, and_40_out, and_32_out);
  xor xor_14 (xor_14_out, xor_6_out, or_6_out);
  or or_7 (or_7_out, and_41_out, and_33_out);
  xor xor_15 (xor_15_out, xor_7_out, or_7_out);
  or or_8 (or_8_out, and_42_out, and_34_out);
  xor xor_16 (xor_16_out, xor_8_out, or_8_out);
  or or_9 (or_9_out, and_43_out, and_35_out);
  and and_44 (and_44_out[0], xor_9_out, and_2_out);
  and and_45 (and_44_out[1], xor_10_out, and_2_out);
  and and_46 (and_44_out[2], xor_11_out, and_2_out);
  and and_47 (and_44_out[3], xor_12_out, and_2_out);
  and and_48 (and_44_out[4], xor_13_out, and_2_out);
  and and_49 (and_44_out[5], xor_14_out, and_2_out);
  and and_50 (and_44_out[6], xor_15_out, and_2_out);
  and and_51 (and_44_out[7], xor_16_out, and_2_out);
  Byte_MUX byte_mux_5 (.select_input(or_10_out), .in_0(and_44_out), .in_1(and_55_out), .out_4(byte_mux_5_out_4));
  or or_10 (or_10_out, right_out, left_out);
  and right (right_out, and_2_out, byte_mux_1_out_4[3]);
  not not_zero (not_zero_out, equals_0_out);
  and and_52 (and_52_out, not_zero_out, and_77_out);
  and left (left_out, and_2_out, byte_mux_1_out_4[4]);
  or smaller_equal (smaller_equal_out, Reg_3_q[7], equals_0_out);
  and and_53 (and_53_out, smaller_equal_out, and_75_out);
  or or_11 (or_11_out, and_52_out, and_53_out, and_62_out);
  and and_54 (and_54_out, and_1_out, or_12_out);
  and and_55 (and_55_out[0], Reg_1_q[1], right_out);
  and and_56 (and_56_out, Reg_1_q[2], right_out);
  and and_57 (and_57_out, Reg_1_q[3], right_out);
  and and_58 (and_58_out, Reg_1_q[4], right_out);
  and and_59 (and_59_out, Reg_1_q[5], right_out);
  and and_60 (and_60_out, Reg_1_q[6], right_out);
  and and_61 (and_61_out, Reg_1_q[7], right_out);
  or greater_eaqual (greater_eaqual_out, greater_0_out, equals_0_out);
  and and_62 (and_62_out, greater_eaqual_out, and_74_out);
  or or_12 (or_12_out, or_11_out, or_13_out);
  and and_63 (and_63_out, Reg_1_q[0], left_out);
  and and_64 (and_64_out, Reg_1_q[1], left_out);
  and and_65 (and_65_out, Reg_1_q[2], left_out);
  and and_66 (and_66_out, Reg_1_q[3], left_out);
  and and_67 (and_67_out, Reg_1_q[4], left_out);
  and and_68 (and_68_out, Reg_1_q[5], left_out);
  and and_69 (and_55_out[7], Reg_1_q[6], left_out);
  and and_70 (and_70_out, Reg_3_q[7], and_73_out);
  and and_71 (and_71_out, equals_0_out, and_76_out);
  or or_13 (or_13_out, and_71_out, and_70_out, and_72_out);
  or or_14 (and_55_out[1], and_63_out, and_56_out);
  or or_15 (and_55_out[2], and_64_out, and_57_out);
  or or_16 (and_55_out[3], and_65_out, and_58_out);
  or or_17 (and_55_out[4], and_66_out, and_59_out);
  or or_18 (and_55_out[5], and_67_out, and_60_out);
  or or_19 (and_55_out[6], and_68_out, and_61_out);
  and and_72 (and_72_out, greater_0_out, nor_10_out);
  and and_73 (and_73_out, nor_11_out, byte_mux_1_out_4[4]);
  and and_74 (and_74_out, nor_12_out, byte_mux_1_out_4[3]);
  and and_75 (and_75_out, byte_mux_1_out_4[3], byte_mux_1_out_4[4], not_20_out);
  and and_76 (and_76_out, nor_13_out, byte_mux_1_out_4[5]);
  and and_77 (and_77_out, byte_mux_1_out_4[3], not_21_out, byte_mux_1_out_4[5]);
  nor nor_10 (nor_10_out, byte_mux_1_out_4[3], byte_mux_1_out_4[4], byte_mux_1_out_4[5]);
  nor nor_11 (nor_11_out, byte_mux_1_out_4[3], byte_mux_1_out_4[5]);
  nor nor_12 (nor_12_out, byte_mux_1_out_4[4], byte_mux_1_out_4[5]);
  not not_20 (not_20_out, byte_mux_1_out_4[5]);
  nor nor_13 (nor_13_out, byte_mux_1_out_4[3], byte_mux_1_out_4[4]);
  not not_21 (not_21_out, byte_mux_1_out_4[4]);
  or or_20 (or_20_out, Reg_3_q[0], Reg_3_q[1], Reg_3_q[2]);
  or or_21 (or_21_out, Reg_3_q[3], Reg_3_q[4], Reg_3_q[5]);
  or or_22 (or_22_out, or_20_out, or_21_out, Reg_3_q[6]);
  not not_22 (not_22_out, Reg_3_q[7]);
  and greater_0 (greater_0_out, or_22_out, not_22_out);
  nor equals_0 (equals_0_out, greater_0_out, Reg_3_q[7]);
  nand nand_1 (nand_1_out[0], Reg_1_q[0], Reg_2_q[0]);
  nand nand_2 (nand_1_out[1], Reg_1_q[1], Reg_2_q[1]);
  nand nand_3 (nand_1_out[2], Reg_1_q[2], Reg_2_q[2]);
  nand nand_4 (nand_1_out[3], Reg_1_q[3], Reg_2_q[3]);
  nand nand_5 (nand_1_out[4], Reg_1_q[4], Reg_2_q[4]);
  nand nand_6 (nand_1_out[5], Reg_1_q[5], Reg_2_q[5]);
  nand nand_7 (nand_1_out[6], Reg_1_q[6], Reg_2_q[6]);
  nand nand_8 (nand_1_out[7], Reg_1_q[7], Reg_2_q[7]);
  and and_78 (and_78_out[0], Reg_1_q[0], Reg_2_q[0]);
  and and_79 (and_78_out[1], Reg_1_q[1], Reg_2_q[1]);
  and and_80 (and_78_out[2], Reg_1_q[2], Reg_2_q[2]);
  and and_81 (and_78_out[3], Reg_1_q[3], Reg_2_q[3]);
  and and_82 (and_78_out[4], Reg_1_q[4], Reg_2_q[4]);
  and and_83 (and_78_out[5], Reg_1_q[5], Reg_2_q[5]);
  and and_84 (and_78_out[6], Reg_1_q[6], Reg_2_q[6]);
  and and_85 (and_78_out[7], Reg_1_q[7], Reg_2_q[7]);
  or or_23 (or_23_out[0], Reg_1_q[0], Reg_2_q[0]);
  or or_24 (or_23_out[1], Reg_1_q[1], Reg_2_q[1]);
  or or_25 (or_23_out[2], Reg_1_q[2], Reg_2_q[2]);
  or or_26 (or_23_out[3], Reg_1_q[3], Reg_2_q[3]);
  or or_27 (or_23_out[4], Reg_1_q[4], Reg_2_q[4]);
  or or_28 (or_23_out[5], Reg_1_q[5], Reg_2_q[5]);
  or or_29 (or_23_out[6], Reg_1_q[6], Reg_2_q[6]);
  or or_30 (or_23_out[7], Reg_1_q[7], Reg_2_q[7]);
  nor nor_14 (nor_14_out[0], Reg_1_q[0], Reg_2_q[0]);
  nor nor_15 (nor_14_out[1], Reg_1_q[1], Reg_2_q[1]);
  nor nor_16 (nor_14_out[2], Reg_1_q[2], Reg_2_q[2]);
  nor nor_17 (nor_14_out[3], Reg_1_q[3], Reg_2_q[3]);
  nor nor_18 (nor_14_out[4], Reg_1_q[4], Reg_2_q[4]);
  nor nor_19 (nor_14_out[5], Reg_1_q[5], Reg_2_q[5]);
  nor nor_20 (nor_14_out[6], Reg_1_q[6], Reg_2_q[6]);
  nor nor_21 (nor_14_out[7], Reg_1_q[7], Reg_2_q[7]);

  // Notes on the sheet:
  //   contents of rom_1 (hex, n*v repeats v):
  //   9 47 1 45 46 9 41 1 42 a3 59 54 68 69 72 85 46 59 62 c0 68 e1
  //   smaller_0
endmodule

module MUX_4_Byte_4_bit_adress (
  input  a_0,
  input  a_1,
  input  a_2,
  input  a_3,
  input  [7:0] b_0,
  input  [7:0] b_1,
  input  [7:0] b_2,
  input  [7:0] b_3,
  output [7:0] out_9
);

  wire or_1_out;
  wire [7:0] byte_mux_1_out_4, byte_mux_2_out_4, byte_switch_1_o, byte_switch_2_o, byte_switch_3_o,
       byte_switch_4_o;

  Byte_switch byte_switch_1 (.i(b_0), .switch(a_0), .o(byte_switch_1_o));
  Byte_switch byte_switch_2 (.i(b_1), .switch(a_1), .o(byte_switch_2_o));
  Byte_switch byte_switch_3 (.i(b_2), .switch(a_2), .o(byte_switch_3_o));
  Byte_switch byte_switch_4 (.i(b_3), .switch(a_3), .o(byte_switch_4_o));
  or or_1 (or_1_out, a_2, a_3);
  Byte_MUX byte_mux_1 (.select_input(a_1), .in_0(byte_switch_1_o), .in_1(byte_switch_2_o), .out_4(byte_mux_1_out_4));
  Byte_MUX byte_mux_2 (.select_input(a_3), .in_0(byte_switch_3_o), .in_1(byte_switch_4_o), .out_4(byte_mux_2_out_4));
  Byte_MUX byte_mux_3 (.select_input(or_1_out), .in_0(byte_mux_1_out_4), .in_1(byte_mux_2_out_4), .out_4(out_9));
endmodule

module Byte_or (
  input  [7:0] in_1,
  input  [7:0] in_2,
  output [7:0] out_3
);

  or or_1 (out_3[0], in_1[0], in_2[0]);
  or or_2 (out_3[1], in_1[1], in_2[1]);
  or or_3 (out_3[2], in_1[2], in_2[2]);
  or or_4 (out_3[3], in_1[3], in_2[3]);
  or or_5 (out_3[4], in_1[4], in_2[4]);
  or or_6 (out_3[5], in_1[5], in_2[5]);
  or or_7 (out_3[6], in_1[6], in_2[6]);
  or or_8 (out_3[7], in_1[7], in_2[7]);
endmodule

module Byte_to_Hex_display (
  input  [7:0] in_1,
  output [3:0] out_2,
  output [3:0] out_3
);


  assign out_2 = in_1[3:0];
  assign out_3 = in_1[7:4];
endmodule

module bit_shifter (
  input  I_16,
  input  I_8,
  input  [7:0] Byte_in,
  output [7:0] Byte_out
);

  wire and_2_out, and_3_out, and_4_out, and_5_out, and_6_out, and_7_out, and_8_out, and_9_out, and_10_out,
       and_11_out, and_12_out, and_13_out, not_1_out, not_2_out, shift_left_out, shift_right_out;

  not not_1 (not_1_out, I_16);
  not not_2 (not_2_out, I_8);
  and shift_right (shift_right_out, not_1_out, I_8);
  and shift_left (shift_left_out, I_16, not_2_out);
  and and_1 (Byte_out[0], Byte_in[1], shift_right_out);
  and and_2 (and_2_out, Byte_in[2], shift_right_out);
  and and_3 (and_3_out, Byte_in[3], shift_right_out);
  and and_4 (and_4_out, Byte_in[4], shift_right_out);
  and and_5 (and_5_out, Byte_in[5], shift_right_out);
  and and_6 (and_6_out, Byte_in[6], shift_right_out);
  and and_7 (and_7_out, Byte_in[7], shift_right_out);
  and and_8 (and_8_out, Byte_in[0], shift_left_out);
  and and_9 (and_9_out, Byte_in[1], shift_left_out);
  and and_10 (and_10_out, Byte_in[2], shift_left_out);
  and and_11 (and_11_out, Byte_in[3], shift_left_out);
  and and_12 (and_12_out, Byte_in[4], shift_left_out);
  and and_13 (and_13_out, Byte_in[5], shift_left_out);
  and and_14 (Byte_out[7], Byte_in[6], shift_left_out);
  or or_1 (Byte_out[1], and_8_out, and_2_out);
  or or_2 (Byte_out[2], and_9_out, and_3_out);
  or or_3 (Byte_out[3], and_10_out, and_4_out);
  or or_4 (Byte_out[4], and_11_out, and_5_out);
  or or_5 (Byte_out[5], and_12_out, and_6_out);
  or or_6 (Byte_out[6], and_13_out, and_7_out);
endmodule
