// Digital circuit 32-bit-switch.dig as structural Verilog
module _32_bit_switch (
  input  [31:0] in,
  input  switch,
  output [31:0] out
);

  and and_1 (out[0], switch, in[0]);
  and and_2 (out[1], switch, in[1]);
  and and_3 (out[2], switch, in[2]);
  and and_4 (out[3], switch, in[3]);
  and and_5 (out[4], switch, in[4]);
  and and_6 (out[5], switch, in[5]);
  and and_7 (out[6], switch, in[6]);
  and and_8 (out[7], switch, in[7]);
  and and_9 (out[8], switch, in[8]);
  and and_10 (out[9], switch, in[9]);
  and and_11 (out[10], switch, in[10]);
  and and_12 (out[11], switch, in[11]);
  and and_13 (out[12], switch, in[12]);
  and and_14 (out[13], switch, in[13]);
  and and_15 (out[14], switch, in[14]);
  and and_16 (out[15], switch, in[15]);
  and and_17 (out[16], switch, in[16]);
  and and_18 (out[17], switch, in[17]);
  and and_19 (out[18], switch, in[18]);
  and and_20 (out[19], switch, in[19]);
  and and_21 (out[20], switch, in[20]);
  and and_22 (out[21], switch, in[21]);
  and and_23 (out[22], switch, in[22]);
  and and_24 (out[23], switch, in[23]);
  and and_25 (out[24], switch, in[24]);
  and and_26 (out[25], switch, in[25]);
  and and_27 (out[26], switch, in[26]);
  and and_28 (out[27], switch, in[27]);
  and and_29 (out[28], switch, in[28]);
  and and_30 (out[29], switch, in[29]);
  and and_31 (out[30], switch, in[30]);
  and and_32 (out[31], switch, in[31]);
endmodule
