// Digital circuit 32_bit_AND.dig as structural Verilog
module _32_bit_AND (
  input  [31:0] i1,
  input  [31:0] i0,
  output [31:0] o
);

  and and_1 (o[0], i1[0], i0[0]);
  and and_2 (o[1], i1[1], i0[1]);
  and and_3 (o[2], i1[2], i0[2]);
  and and_4 (o[3], i1[3], i0[3]);
  and and_5 (o[4], i1[4], i0[4]);
  and and_6 (o[5], i1[5], i0[5]);
  and and_7 (o[6], i1[6], i0[6]);
  and and_8 (o[7], i1[7], i0[7]);
  and and_9 (o[8], i1[8], i0[8]);
  and and_10 (o[9], i1[9], i0[9]);
  and and_11 (o[10], i1[10], i0[10]);
  and and_12 (o[11], i1[11], i0[11]);
  and and_13 (o[12], i1[12], i0[12]);
  and and_14 (o[13], i1[13], i0[13]);
  and and_15 (o[14], i1[14], i0[14]);
  and and_16 (o[15], i1[15], i0[15]);
  and and_17 (o[16], i1[16], i0[16]);
  and and_18 (o[17], i1[17], i0[17]);
  and and_19 (o[18], i1[18], i0[18]);
  and and_20 (o[19], i1[19], i0[19]);
  and and_21 (o[20], i1[20], i0[20]);
  and and_22 (o[21], i1[21], i0[21]);
  and and_23 (o[22], i1[22], i0[22]);
  and and_24 (o[23], i1[23], i0[23]);
  and and_25 (o[24], i1[24], i0[24]);
  and and_26 (o[25], i1[25], i0[25]);
  and and_27 (o[26], i1[26], i0[26]);
  and and_28 (o[27], i1[27], i0[27]);
  and and_29 (o[28], i1[28], i0[28]);
  and and_30 (o[29], i1[29], i0[29]);
  and and_31 (o[30], i1[30], i0[30]);
  and and_32 (o[31], i1[31], i0[31]);
endmodule
