// Digital circuit 32_bit_MUX.dig as structural Verilog
module _32_bit_MUX (
  input  [31:0] in_1,
  input  [31:0] in_2,
  input  select,
  output [31:0] out
);

  wire not_1_out;
  wire [31:0] _32_bit_switch_1_out, _32_bit_switch_2_out;

  _32_bit_switch _32_bit_switch_1 (.in(in_1), .switch(select), .out(_32_bit_switch_1_out));
  _32_bit_switch _32_bit_switch_2 (.in(in_2), .switch(not_1_out), .out(_32_bit_switch_2_out));
  not not_1 (not_1_out, select);
  _32_bit_OR _32_bit_or_1 (.i1(_32_bit_switch_1_out), .i0(_32_bit_switch_2_out), .o(out));
endmodule
