// Digital circuit 32_bit_inverter.dig as structural Verilog
module _32_bit_inverter (
  input  [31:0] inv_in,
  output [31:0] inv_out
);

  not not_1 (inv_out[0], inv_in[0]);
  not not_2 (inv_out[1], inv_in[1]);
  not not_3 (inv_out[2], inv_in[2]);
  not not_4 (inv_out[3], inv_in[3]);
  not not_5 (inv_out[4], inv_in[4]);
  not not_6 (inv_out[5], inv_in[5]);
  not not_7 (inv_out[6], inv_in[6]);
  not not_8 (inv_out[7], inv_in[7]);
  not not_9 (inv_out[8], inv_in[8]);
  not not_10 (inv_out[9], inv_in[9]);
  not not_11 (inv_out[10], inv_in[10]);
  not not_12 (inv_out[11], inv_in[11]);
  not not_13 (inv_out[12], inv_in[12]);
  not not_14 (inv_out[13], inv_in[13]);
  not not_15 (inv_out[14], inv_in[14]);
  not not_16 (inv_out[15], inv_in[15]);
  not not_17 (inv_out[16], inv_in[16]);
  not not_18 (inv_out[17], inv_in[17]);
  not not_19 (inv_out[18], inv_in[18]);
  not not_20 (inv_out[19], inv_in[19]);
  not not_21 (inv_out[20], inv_in[20]);
  not not_22 (inv_out[21], inv_in[21]);
  not not_23 (inv_out[22], inv_in[22]);
  not not_24 (inv_out[23], inv_in[23]);
  not not_25 (inv_out[24], inv_in[24]);
  not not_26 (inv_out[25], inv_in[25]);
  not not_27 (inv_out[26], inv_in[26]);
  not not_28 (inv_out[27], inv_in[27]);
  not not_29 (inv_out[28], inv_in[28]);
  not not_30 (inv_out[29], inv_in[29]);
  not not_31 (inv_out[30], inv_in[30]);
  not not_32 (inv_out[31], inv_in[31]);
endmodule
