// Digital circuit 32_bit_switch.dig as structural Verilog
module _32_bit_switch (
  input  [31:0] i1,
  input  ENA,
  output [31:0] o
);

  and and_1 (o[0], i1[0], ENA);
  and and_2 (o[1], i1[1], ENA);
  and and_3 (o[2], i1[2], ENA);
  and and_4 (o[3], i1[3], ENA);
  and and_5 (o[4], i1[4], ENA);
  and and_6 (o[5], i1[5], ENA);
  and and_7 (o[6], i1[6], ENA);
  and and_8 (o[7], i1[7], ENA);
  and and_9 (o[8], i1[8], ENA);
  and and_10 (o[9], i1[9], ENA);
  and and_11 (o[10], i1[10], ENA);
  and and_12 (o[11], i1[11], ENA);
  and and_13 (o[12], i1[12], ENA);
  and and_14 (o[13], i1[13], ENA);
  and and_15 (o[14], i1[14], ENA);
  and and_16 (o[15], i1[15], ENA);
  and and_17 (o[16], i1[16], ENA);
  and and_18 (o[17], i1[17], ENA);
  and and_19 (o[18], i1[18], ENA);
  and and_20 (o[19], i1[19], ENA);
  and and_21 (o[20], i1[20], ENA);
  and and_22 (o[21], i1[21], ENA);
  and and_23 (o[22], i1[22], ENA);
  and and_24 (o[23], i1[23], ENA);
  and and_25 (o[24], i1[24], ENA);
  and and_26 (o[25], i1[25], ENA);
  and and_27 (o[26], i1[26], ENA);
  and and_28 (o[27], i1[27], ENA);
  and and_29 (o[28], i1[28], ENA);
  and and_30 (o[29], i1[29], ENA);
  and and_31 (o[30], i1[30], ENA);
  and and_32 (o[31], i1[31], ENA);
endmodule
