// Digital circuit full adder.dig as structural Verilog
module full_adder (
  input  [7:0] operand_1,
  input  [7:0] operadn_2,
  input  carry_in,
  output overflow_flag,
  output [7:0] \output 
);

  wire and_1_out, and_2_out, and_3_out, and_4_out, and_5_out, and_6_out, and_7_out, and_8_out, and_9_out,
       and_10_out, and_11_out, and_12_out, and_13_out, and_14_out, and_15_out, and_16_out, or_1_out,
       or_2_out, or_3_out, or_4_out, or_5_out, or_6_out, or_7_out, xor_1_out, xor_2_out, xor_3_out,
       xor_4_out, xor_5_out, xor_6_out, xor_7_out, xor_8_out;

  // full_adder full_adder_1: pin names not known
  xor xor_1 (xor_1_out, operadn_2[0], operand_1[0]);
  and and_1 (and_1_out, operand_1[0], operadn_2[0]);
  xor xor_2 (xor_2_out, operadn_2[1], operand_1[1]);
  and and_2 (and_2_out, operand_1[1], operadn_2[1]);
  xor xor_3 (xor_3_out, operadn_2[2], operand_1[2]);
  and and_3 (and_3_out, operand_1[2], operadn_2[2]);
  xor xor_4 (xor_4_out, operadn_2[3], operand_1[3]);
  and and_4 (and_4_out, operand_1[3], operadn_2[3]);
  xor xor_5 (xor_5_out, operadn_2[4], operand_1[4]);
  and and_5 (and_5_out, operand_1[4], operadn_2[4]);
  xor xor_6 (xor_6_out, operadn_2[5], operand_1[5]);
  and and_6 (and_6_out, operand_1[5], operadn_2[5]);
  xor xor_7 (xor_7_out, operadn_2[6], operand_1[6]);
  and and_7 (and_7_out, operand_1[6], operadn_2[6]);
  xor xor_8 (xor_8_out, operadn_2[7], operand_1[7]);
  and and_8 (and_8_out, operand_1[7], operadn_2[7]);
  and and_9 (and_9_out, xor_1_out, carry_in);
  and and_10 (and_10_out, xor_2_out, or_1_out);
  and and_11 (and_11_out, xor_3_out, or_2_out);
  and and_12 (and_12_out, xor_4_out, or_3_out);
  and and_13 (and_13_out, xor_5_out, or_4_out);
  and and_14 (and_14_out, xor_6_out, or_5_out);
  and and_15 (and_15_out, xor_7_out, or_6_out);
  and and_16 (and_16_out, xor_8_out, or_7_out);
  or or_1 (or_1_out, and_9_out, and_1_out);
  or or_2 (or_2_out, and_10_out, and_2_out);
  or or_3 (or_3_out, and_11_out, and_3_out);
  or or_4 (or_4_out, and_12_out, and_4_out);
  or or_5 (or_5_out, and_13_out, and_5_out);
  or or_6 (or_6_out, and_14_out, and_6_out);
  or or_7 (or_7_out, and_15_out, and_7_out);
  or or_8 (overflow_flag, and_16_out, and_8_out);
  xor xor_9 (\output [0], carry_in, xor_1_out);
  xor xor_10 (\output [1], or_1_out, xor_2_out);
  xor xor_11 (\output [2], or_2_out, xor_3_out);
  xor xor_12 (\output [3], or_3_out, xor_4_out);
  xor xor_13 (\output [4], or_4_out, xor_5_out);
  xor xor_14 (\output [5], or_5_out, xor_6_out);
  xor xor_15 (\output [6], or_6_out, xor_7_out);
  xor xor_16 (\output [7], or_7_out, xor_8_out);
endmodule
