// Digital circuit full_adder.dig as structural Verilog
module full_adder (
  input  I1,
  input  I2,
  input  C,
  input  [31:0] B,
  input  [31:0] A,
  input  carry_in,
  input  F1,
  input  F0,
  input  ENB,
  input  ENA,
  input  INVA,
  output o1,
  output c_2,
  output carry_flag,
  output [31:0] \output ,
  output [31:0] out_16,
  output [31:0] out_17
);

  wire and_1_out, and_2_out, and_3_out, and_4_out, and_5_out, and_6_out, and_7_out, and_8_out, and_9_out,
       and_10_out, and_11_out, and_12_out, and_13_out, and_14_out, and_15_out, and_16_out, and_17_out,
       and_18_out, and_19_out, and_20_out, and_21_out, and_22_out, and_47_out, and_48_out, and_49_out,
       and_50_out, and_51_out, and_52_out, and_53_out, and_54_out, and_55_out, and_56_out, and_57_out,
       and_58_out, and_59_out, and_60_out, and_61_out, and_62_out, and_87_out, and_88_out, and_89_out,
       and_90_out, and_91_out, and_92_out, and_93_out, and_94_out, and_119_out, and_120_out, and_121_out,
       and_122_out, and_123_out, and_124_out, and_125_out, and_126_out, and_127_out, and_128_out,
       and_129_out, and_130_out, and_131_out, and_132_out, and_133_out, and_134_out, and_135_out,
       and_136_out, and_137_out, and_138_out, and_139_out, and_140_out, and_141_out, and_142_out, not_1_out,
       not_2_out, or_2_out, or_3_out, or_4_out, or_5_out, or_6_out, or_7_out, or_8_out, or_9_out, or_42_out,
       or_43_out, or_44_out, or_45_out, or_46_out, or_47_out, or_48_out, or_49_out, or_74_out, or_75_out,
       or_76_out, or_77_out, or_78_out, or_79_out, or_80_out, or_81_out, or_82_out, or_83_out, or_84_out,
       or_85_out, or_86_out, or_87_out, or_88_out, xor_1_out, xor_3_out, xor_4_out, xor_5_out, xor_6_out,
       xor_7_out, xor_8_out, xor_9_out, xor_10_out, xor_19_out, xor_20_out, xor_21_out, xor_22_out,
       xor_23_out, xor_24_out, xor_25_out, xor_26_out, xor_35_out, xor_36_out, xor_37_out, xor_38_out,
       xor_39_out, xor_40_out, xor_41_out, xor_42_out, xor_51_out, xor_52_out, xor_53_out, xor_54_out,
       xor_55_out, xor_56_out, xor_57_out, xor_58_out;
  wire [31:0] _32_bit_inverter_1_inv_out, _32_bit_mux_1_out, _32_bit_switch_1_out, _32_bit_switch_2_out;

  xor xor_1 (xor_1_out, I2, I1);
  and and_1 (and_1_out, I1, I2);
  and and_2 (and_2_out, xor_1_out, C);
  xor xor_2 (o1, C, xor_1_out);
  or or_1 (c_2, and_2_out, and_1_out);
  not not_1 (not_1_out, F0);
  not not_2 (not_2_out, F1);
  _32_bit_inverter _32_bit_inverter_1 (.inv_in(A), .inv_out(_32_bit_inverter_1_inv_out));
  _32_bit_switch _32_bit_switch_1 (.in(A), .switch(ENA), .out(_32_bit_switch_1_out));
  _32_bit_switch _32_bit_switch_2 (.in(B), .switch(ENB), .out(_32_bit_switch_2_out));
  and and_3 (and_3_out, F0, F1);
  _32_bit_MUX _32_bit_mux_1 (
    .in_1(_32_bit_inverter_1_inv_out), .in_2(_32_bit_switch_1_out), .select(INVA), .out(_32_bit_mux_1_out));
  and and_4 (and_4_out, F0, not_2_out);
  and and_5 (and_5_out, not_1_out, F1);
  and and_6 (and_6_out, not_1_out, not_2_out);
  xor xor_3 (xor_3_out, _32_bit_mux_1_out[24], _32_bit_switch_2_out[24]);
  and and_7 (and_7_out, _32_bit_switch_2_out[24], _32_bit_mux_1_out[24]);
  xor xor_4 (xor_4_out, _32_bit_mux_1_out[25], _32_bit_switch_2_out[25]);
  and and_8 (and_8_out, _32_bit_switch_2_out[25], _32_bit_mux_1_out[25]);
  xor xor_5 (xor_5_out, _32_bit_mux_1_out[26], _32_bit_switch_2_out[26]);
  and and_9 (and_9_out, _32_bit_switch_2_out[26], _32_bit_mux_1_out[26]);
  xor xor_6 (xor_6_out, _32_bit_mux_1_out[27], _32_bit_switch_2_out[27]);
  and and_10 (and_10_out, _32_bit_switch_2_out[27], _32_bit_mux_1_out[27]);
  xor xor_7 (xor_7_out, _32_bit_mux_1_out[28], _32_bit_switch_2_out[28]);
  and and_11 (and_11_out, _32_bit_switch_2_out[28], _32_bit_mux_1_out[28]);
  xor xor_8 (xor_8_out, _32_bit_mux_1_out[29], _32_bit_switch_2_out[29]);
  and and_12 (and_12_out, _32_bit_switch_2_out[29], _32_bit_mux_1_out[29]);
  xor xor_9 (xor_9_out, _32_bit_mux_1_out[30], _32_bit_switch_2_out[30]);
  and and_13 (and_13_out, _32_bit_switch_2_out[30], _32_bit_mux_1_out[30]);
  xor xor_10 (xor_10_out, _32_bit_mux_1_out[31], _32_bit_switch_2_out[31]);
  and and_14 (and_14_out, _32_bit_switch_2_out[31], _32_bit_mux_1_out[31]);
  and and_15 (and_15_out, xor_3_out, carry_in);
  and and_16 (and_16_out, xor_4_out, or_2_out);
  and and_17 (and_17_out, xor_5_out, or_3_out);
  and and_18 (and_18_out, xor_6_out, or_4_out);
  and and_19 (and_19_out, xor_7_out, or_5_out);
  and and_20 (and_20_out, xor_8_out, or_6_out);
  and and_21 (and_21_out, xor_9_out, or_7_out);
  and and_22 (and_22_out, xor_10_out, or_8_out);
  xor xor_11 (\output [24], carry_in, xor_3_out);
  or or_2 (or_2_out, and_15_out, and_7_out);
  xor xor_12 (\output [25], or_2_out, xor_4_out);
  or or_3 (or_3_out, and_16_out, and_8_out);
  xor xor_13 (\output [26], or_3_out, xor_5_out);
  or or_4 (or_4_out, and_17_out, and_9_out);
  xor xor_14 (\output [27], or_4_out, xor_6_out);
  or or_5 (or_5_out, and_18_out, and_10_out);
  xor xor_15 (\output [28], or_5_out, xor_7_out);
  or or_6 (or_6_out, and_19_out, and_11_out);
  xor xor_16 (\output [29], or_6_out, xor_8_out);
  or or_7 (or_7_out, and_20_out, and_12_out);
  xor xor_17 (\output [30], or_7_out, xor_9_out);
  or or_8 (or_8_out, and_21_out, and_13_out);
  xor xor_18 (\output [31], or_8_out, xor_10_out);
  or or_9 (or_9_out, and_22_out, and_14_out);
  or or_10 (out_17[0], _32_bit_mux_1_out[0], _32_bit_switch_2_out[0]);
  or or_11 (out_17[0], _32_bit_mux_1_out[0], _32_bit_switch_2_out[0]);
  or or_12 (out_17[1], _32_bit_mux_1_out[1], _32_bit_switch_2_out[1]);
  or or_13 (out_17[1], _32_bit_mux_1_out[1], _32_bit_switch_2_out[1]);
  or or_14 (out_17[2], _32_bit_mux_1_out[2], _32_bit_switch_2_out[2]);
  or or_15 (out_17[2], _32_bit_mux_1_out[2], _32_bit_switch_2_out[2]);
  or or_16 (out_17[3], _32_bit_mux_1_out[3], _32_bit_switch_2_out[3]);
  or or_17 (out_17[3], _32_bit_mux_1_out[3], _32_bit_switch_2_out[3]);
  or or_18 (out_17[4], _32_bit_mux_1_out[4], _32_bit_switch_2_out[4]);
  or or_19 (out_17[4], _32_bit_mux_1_out[4], _32_bit_switch_2_out[4]);
  or or_20 (out_17[5], _32_bit_mux_1_out[5], _32_bit_switch_2_out[5]);
  or or_21 (out_17[5], _32_bit_mux_1_out[5], _32_bit_switch_2_out[5]);
  or or_22 (out_17[6], _32_bit_mux_1_out[6], _32_bit_switch_2_out[6]);
  or or_23 (out_17[6], _32_bit_mux_1_out[6], _32_bit_switch_2_out[6]);
  or or_24 (out_17[7], _32_bit_mux_1_out[7], _32_bit_switch_2_out[7]);
  or or_25 (out_17[7], _32_bit_mux_1_out[7], _32_bit_switch_2_out[7]);
  and and_23 (out_16[0], _32_bit_mux_1_out[0], _32_bit_switch_2_out[0]);
  and and_24 (out_16[1], _32_bit_mux_1_out[1], _32_bit_switch_2_out[1]);
  and and_25 (out_16[2], _32_bit_mux_1_out[2], _32_bit_switch_2_out[2]);
  and and_26 (out_16[3], _32_bit_mux_1_out[3], _32_bit_switch_2_out[3]);
  and and_27 (out_16[4], _32_bit_mux_1_out[4], _32_bit_switch_2_out[4]);
  and and_28 (out_16[5], _32_bit_mux_1_out[5], _32_bit_switch_2_out[5]);
  and and_29 (out_16[6], _32_bit_mux_1_out[6], _32_bit_switch_2_out[6]);
  and and_30 (out_16[7], _32_bit_mux_1_out[7], _32_bit_switch_2_out[7]);
  or or_26 (out_17[8], _32_bit_mux_1_out[8], _32_bit_switch_2_out[8]);
  or or_27 (out_17[8], _32_bit_mux_1_out[8], _32_bit_switch_2_out[8]);
  or or_28 (out_17[9], _32_bit_mux_1_out[9], _32_bit_switch_2_out[9]);
  or or_29 (out_17[9], _32_bit_mux_1_out[9], _32_bit_switch_2_out[9]);
  or or_30 (out_17[10], _32_bit_mux_1_out[10], _32_bit_switch_2_out[10]);
  or or_31 (out_17[10], _32_bit_mux_1_out[10], _32_bit_switch_2_out[10]);
  or or_32 (out_17[11], _32_bit_mux_1_out[11], _32_bit_switch_2_out[11]);
  or or_33 (out_17[11], _32_bit_mux_1_out[11], _32_bit_switch_2_out[11]);
  or or_34 (out_17[12], _32_bit_mux_1_out[12], _32_bit_switch_2_out[12]);
  or or_35 (out_17[12], _32_bit_mux_1_out[12], _32_bit_switch_2_out[12]);
  or or_36 (out_17[13], _32_bit_mux_1_out[13], _32_bit_switch_2_out[13]);
  or or_37 (out_17[13], _32_bit_mux_1_out[13], _32_bit_switch_2_out[13]);
  or or_38 (out_17[14], _32_bit_mux_1_out[14], _32_bit_switch_2_out[14]);
  or or_39 (out_17[14], _32_bit_mux_1_out[14], _32_bit_switch_2_out[14]);
  or or_40 (out_17[15], _32_bit_mux_1_out[15], _32_bit_switch_2_out[15]);
  or or_41 (out_17[15], _32_bit_mux_1_out[15], _32_bit_switch_2_out[15]);
  and and_31 (out_16[8], _32_bit_mux_1_out[8], _32_bit_switch_2_out[8]);
  and and_32 (out_16[8], _32_bit_mux_1_out[8], _32_bit_switch_2_out[8]);
  and and_33 (out_16[9], _32_bit_mux_1_out[9], _32_bit_switch_2_out[9]);
  and and_34 (out_16[9], _32_bit_mux_1_out[9], _32_bit_switch_2_out[9]);
  and and_35 (out_16[10], _32_bit_mux_1_out[10], _32_bit_switch_2_out[10]);
  and and_36 (out_16[10], _32_bit_mux_1_out[10], _32_bit_switch_2_out[10]);
  and and_37 (out_16[11], _32_bit_mux_1_out[11], _32_bit_switch_2_out[11]);
  and and_38 (out_16[11], _32_bit_mux_1_out[11], _32_bit_switch_2_out[11]);
  and and_39 (out_16[12], _32_bit_mux_1_out[12], _32_bit_switch_2_out[12]);
  and and_40 (out_16[12], _32_bit_mux_1_out[12], _32_bit_switch_2_out[12]);
  and and_41 (out_16[13], _32_bit_mux_1_out[13], _32_bit_switch_2_out[13]);
  and and_42 (out_16[13], _32_bit_mux_1_out[13], _32_bit_switch_2_out[13]);
  and and_43 (out_16[14], _32_bit_mux_1_out[14], _32_bit_switch_2_out[14]);
  and and_44 (out_16[14], _32_bit_mux_1_out[14], _32_bit_switch_2_out[14]);
  and and_45 (out_16[15], _32_bit_mux_1_out[15], _32_bit_switch_2_out[15]);
  and and_46 (out_16[15], _32_bit_mux_1_out[15], _32_bit_switch_2_out[15]);
  xor xor_19 (xor_19_out, _32_bit_mux_1_out[16], _32_bit_switch_2_out[16]);
  and and_47 (and_47_out, _32_bit_switch_2_out[16], _32_bit_mux_1_out[16]);
  xor xor_20 (xor_20_out, _32_bit_mux_1_out[17], _32_bit_switch_2_out[17]);
  and and_48 (and_48_out, _32_bit_switch_2_out[17], _32_bit_mux_1_out[17]);
  xor xor_21 (xor_21_out, _32_bit_mux_1_out[18], _32_bit_switch_2_out[18]);
  and and_49 (and_49_out, _32_bit_switch_2_out[18], _32_bit_mux_1_out[18]);
  xor xor_22 (xor_22_out, _32_bit_mux_1_out[19], _32_bit_switch_2_out[19]);
  and and_50 (and_50_out, _32_bit_switch_2_out[19], _32_bit_mux_1_out[19]);
  xor xor_23 (xor_23_out, _32_bit_mux_1_out[20], _32_bit_switch_2_out[20]);
  and and_51 (and_51_out, _32_bit_switch_2_out[20], _32_bit_mux_1_out[20]);
  xor xor_24 (xor_24_out, _32_bit_mux_1_out[21], _32_bit_switch_2_out[21]);
  and and_52 (and_52_out, _32_bit_switch_2_out[21], _32_bit_mux_1_out[21]);
  xor xor_25 (xor_25_out, _32_bit_mux_1_out[22], _32_bit_switch_2_out[22]);
  and and_53 (and_53_out, _32_bit_switch_2_out[22], _32_bit_mux_1_out[22]);
  xor xor_26 (xor_26_out, _32_bit_mux_1_out[23], _32_bit_switch_2_out[23]);
  and and_54 (and_54_out, _32_bit_switch_2_out[23], _32_bit_mux_1_out[23]);
  and and_55 (and_55_out, xor_19_out, or_9_out);
  and and_56 (and_56_out, xor_20_out, or_42_out);
  and and_57 (and_57_out, xor_21_out, or_43_out);
  and and_58 (and_58_out, xor_22_out, or_44_out);
  and and_59 (and_59_out, xor_23_out, or_45_out);
  and and_60 (and_60_out, xor_24_out, or_46_out);
  and and_61 (and_61_out, xor_25_out, or_47_out);
  and and_62 (and_62_out, xor_26_out, or_48_out);
  xor xor_27 (\output [16], or_9_out, xor_19_out);
  or or_42 (or_42_out, and_55_out, and_47_out);
  xor xor_28 (\output [17], or_42_out, xor_20_out);
  or or_43 (or_43_out, and_56_out, and_48_out);
  xor xor_29 (\output [18], or_43_out, xor_21_out);
  or or_44 (or_44_out, and_57_out, and_49_out);
  xor xor_30 (\output [19], or_44_out, xor_22_out);
  or or_45 (or_45_out, and_58_out, and_50_out);
  xor xor_31 (\output [20], or_45_out, xor_23_out);
  or or_46 (or_46_out, and_59_out, and_51_out);
  xor xor_32 (\output [21], or_46_out, xor_24_out);
  or or_47 (or_47_out, and_60_out, and_52_out);
  xor xor_33 (\output [22], or_47_out, xor_25_out);
  or or_48 (or_48_out, and_61_out, and_53_out);
  xor xor_34 (\output [23], or_48_out, xor_26_out);
  or or_49 (or_49_out, and_62_out, and_54_out);
  or or_50 (out_17[16], _32_bit_mux_1_out[16], _32_bit_switch_2_out[16]);
  or or_51 (out_17[16], _32_bit_mux_1_out[16], _32_bit_switch_2_out[16]);
  or or_52 (out_17[17], _32_bit_mux_1_out[17], _32_bit_switch_2_out[17]);
  or or_53 (out_17[17], _32_bit_mux_1_out[17], _32_bit_switch_2_out[17]);
  or or_54 (out_17[18], _32_bit_mux_1_out[18], _32_bit_switch_2_out[18]);
  or or_55 (out_17[18], _32_bit_mux_1_out[18], _32_bit_switch_2_out[18]);
  or or_56 (out_17[19], _32_bit_mux_1_out[19], _32_bit_switch_2_out[19]);
  or or_57 (out_17[19], _32_bit_mux_1_out[19], _32_bit_switch_2_out[19]);
  or or_58 (out_17[20], _32_bit_mux_1_out[20], _32_bit_switch_2_out[20]);
  or or_59 (out_17[20], _32_bit_mux_1_out[20], _32_bit_switch_2_out[20]);
  or or_60 (out_17[21], _32_bit_mux_1_out[21], _32_bit_switch_2_out[21]);
  or or_61 (out_17[21], _32_bit_mux_1_out[21], _32_bit_switch_2_out[21]);
  or or_62 (out_17[22], _32_bit_mux_1_out[22], _32_bit_switch_2_out[22]);
  or or_63 (out_17[22], _32_bit_mux_1_out[22], _32_bit_switch_2_out[22]);
  or or_64 (out_17[23], _32_bit_mux_1_out[23], _32_bit_switch_2_out[23]);
  or or_65 (out_17[23], _32_bit_mux_1_out[23], _32_bit_switch_2_out[23]);
  and and_63 (out_16[16], _32_bit_mux_1_out[16], _32_bit_switch_2_out[16]);
  and and_64 (out_16[16], _32_bit_mux_1_out[16], _32_bit_switch_2_out[16]);
  and and_65 (out_16[16], _32_bit_mux_1_out[16], _32_bit_switch_2_out[16]);
  and and_66 (out_16[17], _32_bit_mux_1_out[17], _32_bit_switch_2_out[17]);
  and and_67 (out_16[17], _32_bit_mux_1_out[17], _32_bit_switch_2_out[17]);
  and and_68 (out_16[17], _32_bit_mux_1_out[17], _32_bit_switch_2_out[17]);
  and and_69 (out_16[18], _32_bit_mux_1_out[18], _32_bit_switch_2_out[18]);
  and and_70 (out_16[18], _32_bit_mux_1_out[18], _32_bit_switch_2_out[18]);
  and and_71 (out_16[18], _32_bit_mux_1_out[18], _32_bit_switch_2_out[18]);
  and and_72 (out_16[19], _32_bit_mux_1_out[19], _32_bit_switch_2_out[19]);
  and and_73 (out_16[19], _32_bit_mux_1_out[19], _32_bit_switch_2_out[19]);
  and and_74 (out_16[19], _32_bit_mux_1_out[19], _32_bit_switch_2_out[19]);
  and and_75 (out_16[20], _32_bit_mux_1_out[20], _32_bit_switch_2_out[20]);
  and and_76 (out_16[20], _32_bit_mux_1_out[20], _32_bit_switch_2_out[20]);
  and and_77 (out_16[20], _32_bit_mux_1_out[20], _32_bit_switch_2_out[20]);
  and and_78 (out_16[21], _32_bit_mux_1_out[21], _32_bit_switch_2_out[21]);
  and and_79 (out_16[21], _32_bit_mux_1_out[21], _32_bit_switch_2_out[21]);
  and and_80 (out_16[21], _32_bit_mux_1_out[21], _32_bit_switch_2_out[21]);
  and and_81 (out_16[22], _32_bit_mux_1_out[22], _32_bit_switch_2_out[22]);
  and and_82 (out_16[22], _32_bit_mux_1_out[22], _32_bit_switch_2_out[22]);
  and and_83 (out_16[22], _32_bit_mux_1_out[22], _32_bit_switch_2_out[22]);
  and and_84 (out_16[23], _32_bit_mux_1_out[23], _32_bit_switch_2_out[23]);
  and and_85 (out_16[23], _32_bit_mux_1_out[23], _32_bit_switch_2_out[23]);
  and and_86 (out_16[23], _32_bit_mux_1_out[23], _32_bit_switch_2_out[23]);
  xor xor_35 (xor_35_out, _32_bit_mux_1_out[8], _32_bit_switch_2_out[8]);
  and and_87 (and_87_out, _32_bit_switch_2_out[8], _32_bit_mux_1_out[8]);
  xor xor_36 (xor_36_out, _32_bit_mux_1_out[9], _32_bit_switch_2_out[9]);
  and and_88 (and_88_out, _32_bit_switch_2_out[9], _32_bit_mux_1_out[9]);
  xor xor_37 (xor_37_out, _32_bit_mux_1_out[10], _32_bit_switch_2_out[10]);
  and and_89 (and_89_out, _32_bit_switch_2_out[10], _32_bit_mux_1_out[10]);
  xor xor_38 (xor_38_out, _32_bit_mux_1_out[11], _32_bit_switch_2_out[11]);
  and and_90 (and_90_out, _32_bit_switch_2_out[11], _32_bit_mux_1_out[11]);
  xor xor_39 (xor_39_out, _32_bit_mux_1_out[12], _32_bit_switch_2_out[12]);
  and and_91 (and_91_out, _32_bit_switch_2_out[12], _32_bit_mux_1_out[12]);
  xor xor_40 (xor_40_out, _32_bit_mux_1_out[13], _32_bit_switch_2_out[13]);
  and and_92 (and_92_out, _32_bit_switch_2_out[13], _32_bit_mux_1_out[13]);
  xor xor_41 (xor_41_out, _32_bit_mux_1_out[14], _32_bit_switch_2_out[14]);
  and and_93 (and_93_out, _32_bit_switch_2_out[14], _32_bit_mux_1_out[14]);
  xor xor_42 (xor_42_out, _32_bit_mux_1_out[15], _32_bit_switch_2_out[15]);
  and and_94 (and_94_out, _32_bit_switch_2_out[15], _32_bit_mux_1_out[15]);
  or or_66 (out_17[24], _32_bit_mux_1_out[24], _32_bit_switch_2_out[24]);
  or or_67 (out_17[25], _32_bit_mux_1_out[25], _32_bit_switch_2_out[25]);
  or or_68 (out_17[26], _32_bit_mux_1_out[26], _32_bit_switch_2_out[26]);
  or or_69 (out_17[27], _32_bit_mux_1_out[27], _32_bit_switch_2_out[27]);
  or or_70 (out_17[28], _32_bit_mux_1_out[28], _32_bit_switch_2_out[28]);
  or or_71 (out_17[29], _32_bit_mux_1_out[29], _32_bit_switch_2_out[29]);
  or or_72 (out_17[30], _32_bit_mux_1_out[30], _32_bit_switch_2_out[30]);
  or or_73 (out_17[31], _32_bit_mux_1_out[31], _32_bit_switch_2_out[31]);
  and and_95 (out_16[24], _32_bit_mux_1_out[24], _32_bit_switch_2_out[24]);
  and and_96 (out_16[24], _32_bit_mux_1_out[24], _32_bit_switch_2_out[24]);
  and and_97 (out_16[24], _32_bit_mux_1_out[24], _32_bit_switch_2_out[24]);
  and and_98 (out_16[25], _32_bit_mux_1_out[25], _32_bit_switch_2_out[25]);
  and and_99 (out_16[25], _32_bit_mux_1_out[25], _32_bit_switch_2_out[25]);
  and and_100 (out_16[25], _32_bit_mux_1_out[25], _32_bit_switch_2_out[25]);
  and and_101 (out_16[26], _32_bit_mux_1_out[26], _32_bit_switch_2_out[26]);
  and and_102 (out_16[26], _32_bit_mux_1_out[26], _32_bit_switch_2_out[26]);
  and and_103 (out_16[26], _32_bit_mux_1_out[26], _32_bit_switch_2_out[26]);
  and and_104 (out_16[27], _32_bit_mux_1_out[27], _32_bit_switch_2_out[27]);
  and and_105 (out_16[27], _32_bit_mux_1_out[27], _32_bit_switch_2_out[27]);
  and and_106 (out_16[27], _32_bit_mux_1_out[27], _32_bit_switch_2_out[27]);
  and and_107 (out_16[28], _32_bit_mux_1_out[28], _32_bit_switch_2_out[28]);
  and and_108 (out_16[28], _32_bit_mux_1_out[28], _32_bit_switch_2_out[28]);
  and and_109 (out_16[28], _32_bit_mux_1_out[28], _32_bit_switch_2_out[28]);
  and and_110 (out_16[29], _32_bit_mux_1_out[29], _32_bit_switch_2_out[29]);
  and and_111 (out_16[29], _32_bit_mux_1_out[29], _32_bit_switch_2_out[29]);
  and and_112 (out_16[29], _32_bit_mux_1_out[29], _32_bit_switch_2_out[29]);
  and and_113 (out_16[30], _32_bit_mux_1_out[30], _32_bit_switch_2_out[30]);
  and and_114 (out_16[30], _32_bit_mux_1_out[30], _32_bit_switch_2_out[30]);
  and and_115 (out_16[30], _32_bit_mux_1_out[30], _32_bit_switch_2_out[30]);
  and and_116 (out_16[31], _32_bit_mux_1_out[31], _32_bit_switch_2_out[31]);
  and and_117 (out_16[31], _32_bit_mux_1_out[31], _32_bit_switch_2_out[31]);
  and and_118 (out_16[31], _32_bit_mux_1_out[31], _32_bit_switch_2_out[31]);
  and and_119 (and_119_out, xor_35_out, or_49_out);
  and and_120 (and_120_out, xor_36_out, or_74_out);
  and and_121 (and_121_out, xor_37_out, or_75_out);
  and and_122 (and_122_out, xor_38_out, or_76_out);
  and and_123 (and_123_out, xor_39_out, or_77_out);
  and and_124 (and_124_out, xor_40_out, or_78_out);
  and and_125 (and_125_out, xor_41_out, or_79_out);
  and and_126 (and_126_out, xor_42_out, or_80_out);
  xor xor_43 (\output [8], or_49_out, xor_35_out);
  or or_74 (or_74_out, and_119_out, and_87_out);
  xor xor_44 (\output [9], or_74_out, xor_36_out);
  or or_75 (or_75_out, and_120_out, and_88_out);
  xor xor_45 (\output [10], or_75_out, xor_37_out);
  or or_76 (or_76_out, and_121_out, and_89_out);
  xor xor_46 (\output [11], or_76_out, xor_38_out);
  or or_77 (or_77_out, and_122_out, and_90_out);
  xor xor_47 (\output [12], or_77_out, xor_39_out);
  or or_78 (or_78_out, and_123_out, and_91_out);
  xor xor_48 (\output [13], or_78_out, xor_40_out);
  or or_79 (or_79_out, and_124_out, and_92_out);
  xor xor_49 (\output [14], or_79_out, xor_41_out);
  or or_80 (or_80_out, and_125_out, and_93_out);
  xor xor_50 (\output [15], or_80_out, xor_42_out);
  or or_81 (or_81_out, and_126_out, and_94_out);
  xor xor_51 (xor_51_out, _32_bit_mux_1_out[0], _32_bit_switch_2_out[0]);
  and and_127 (and_127_out, _32_bit_switch_2_out[0], _32_bit_mux_1_out[0]);
  xor xor_52 (xor_52_out, _32_bit_mux_1_out[1], _32_bit_switch_2_out[1]);
  and and_128 (and_128_out, _32_bit_switch_2_out[1], _32_bit_mux_1_out[1]);
  xor xor_53 (xor_53_out, _32_bit_mux_1_out[2], _32_bit_switch_2_out[2]);
  and and_129 (and_129_out, _32_bit_switch_2_out[2], _32_bit_mux_1_out[2]);
  xor xor_54 (xor_54_out, _32_bit_mux_1_out[3], _32_bit_switch_2_out[3]);
  and and_130 (and_130_out, _32_bit_switch_2_out[3], _32_bit_mux_1_out[3]);
  xor xor_55 (xor_55_out, _32_bit_mux_1_out[4], _32_bit_switch_2_out[4]);
  and and_131 (and_131_out, _32_bit_switch_2_out[4], _32_bit_mux_1_out[4]);
  xor xor_56 (xor_56_out, _32_bit_mux_1_out[5], _32_bit_switch_2_out[5]);
  and and_132 (and_132_out, _32_bit_switch_2_out[5], _32_bit_mux_1_out[5]);
  xor xor_57 (xor_57_out, _32_bit_mux_1_out[6], _32_bit_switch_2_out[6]);
  and and_133 (and_133_out, _32_bit_switch_2_out[6], _32_bit_mux_1_out[6]);
  xor xor_58 (xor_58_out, _32_bit_mux_1_out[7], _32_bit_switch_2_out[7]);
  and and_134 (and_134_out, _32_bit_switch_2_out[7], _32_bit_mux_1_out[7]);
  and and_135 (and_135_out, xor_51_out, or_81_out);
  and and_136 (and_136_out, xor_52_out, or_82_out);
  and and_137 (and_137_out, xor_53_out, or_83_out);
  and and_138 (and_138_out, xor_54_out, or_84_out);
  and and_139 (and_139_out, xor_55_out, or_85_out);
  and and_140 (and_140_out, xor_56_out, or_86_out);
  and and_141 (and_141_out, xor_57_out, or_87_out);
  and and_142 (and_142_out, xor_58_out, or_88_out);
  xor xor_59 (\output [0], or_81_out, xor_51_out);
  or or_82 (or_82_out, and_135_out, and_127_out);
  xor xor_60 (\output [1], or_82_out, xor_52_out);
  or or_83 (or_83_out, and_136_out, and_128_out);
  xor xor_61 (\output [2], or_83_out, xor_53_out);
  or or_84 (or_84_out, and_137_out, and_129_out);
  xor xor_62 (\output [3], or_84_out, xor_54_out);
  or or_85 (or_85_out, and_138_out, and_130_out);
  xor xor_63 (\output [4], or_85_out, xor_55_out);
  or or_86 (or_86_out, and_139_out, and_131_out);
  xor xor_64 (\output [5], or_86_out, xor_56_out);
  or or_87 (or_87_out, and_140_out, and_132_out);
  xor xor_65 (\output [6], or_87_out, xor_57_out);
  or or_88 (or_88_out, and_141_out, and_133_out);
  xor xor_66 (\output [7], or_88_out, xor_58_out);
  or or_89 (carry_flag, and_142_out, and_134_out);
endmodule

/* Test case adder_test:
I1 I2 C o1 c
0 0 0 0 0
0 0 1 1 0
0 1 0 1 0
0 1 1 0 1
1 0 0 1 0
1 0 1 0 1
1 1 0 0 1
1 1 1 1 1
*/
