// Digital circuit random.dig as structural Verilog
module random (
  input  in_1,
  input  in_2,
  input  in_3
);

  wire and_1_out, nand_1_out, nand_2_out, nand_3_out, nand_4_out, nand_5_out, nand_6_out;

  nand nand_1 (nand_1_out, in_1, in_2);
  nand nand_2 (nand_2_out, in_1, in_2);
  nand nand_3 (nand_3_out, in_3, in_3);
  and and_1 (and_1_out, nand_1_out, nand_2_out);
  nand nand_4 (nand_4_out, and_1_out, and_1_out);
  nand nand_5 (nand_5_out, nand_3_out, nand_3_out);
  nand nand_6 (nand_6_out, nand_4_out, nand_5_out);
  LED led_1 (.in(nand_6_out));
endmodule
