// Logisim project cpu.circ as structural Verilog
module main (
  input  [7:0] data,
  input  [7:0] instruction,
  input  [7:0] adress,
  input  activate,
  output [7:0] out_5,
  output [7:0] out_6,
  output [7:0] out_7,
  output [7:0] out_8,
  output out_9
);

  wire adress_decoder_adress_0, adress_decoder_adress_1, adress_decoder_adress_2, adress_decoder_adress_3,
       clock_1_out, Instruction_decoder_addition, Instruction_decoder_subtraction, or_1_out, or_2_out,
       temp_1_out_2;
  wire [7:0] byte_inverter_1_out_2, byte_mux_1_out_4, byte_mux_2_out_4, byte_mux_3_out_4, byte_mux_4_out_4,
       byte_switch_2_o, byte_switch_3_o, byte_switch_4_o, byte_switch_5_o, byte_switch_6_o, byte_switch_7_o,
       byter_adder_1_o_1, mux_4_byte_2_out_6, reg_0_q, reg_1_q, reg_2_q, reg_3_q;

  temp temp_1 (.in_1(instruction), .out_2(temp_1_out_2));
  Byte_MUX byte_mux_1 (.select_input(temp_1_out_2), .in_0(data), .in_1(out_6), .out_4(byte_mux_1_out_4));
  Byte_switch byte_switch_1 (.i(byte_mux_1_out_4), .switch(activate), .o(out_5));
  Byte_switch byte_switch_2 (.i(instruction), .switch(activate), .o(byte_switch_2_o));
  Byte_switch byte_switch_3 (.i(adress), .switch(activate), .o(byte_switch_3_o));
  Byte_MUX byte_mux_2 (
    .select_input(byte_switch_2_o[1]), .in_0(byte_mux_1_out_4), .in_1(mux_4_byte_2_out_6),
    .out_4(byte_mux_2_out_4));
  or or_1 (or_1_out, adress_decoder_adress_3, or_2_out);
  Adress_dcoder adress_decoder (
    .in_1(byte_switch_3_o), .adress_0(adress_decoder_adress_0), .adress_1(adress_decoder_adress_1),
    .adress_2(adress_decoder_adress_2), .adress_3(adress_decoder_adress_3));
  Clock clock_1 (.out(clock_1_out));
  Register reg_0 (.D(byte_mux_2_out_4), .en(adress_decoder_adress_0), .clk(clock_1_out), .Q(reg_0_q));  // open: clr
  Register reg_1 (.D(byte_mux_2_out_4), .en(adress_decoder_adress_1), .clk(clock_1_out), .Q(reg_1_q));  // open: clr
  Register reg_2 (.D(byte_mux_2_out_4), .en(adress_decoder_adress_2), .clk(clock_1_out), .Q(reg_2_q));  // open: clr
  Register reg_3 (.D(byte_mux_3_out_4), .en(or_1_out), .clk(clock_1_out), .Q(reg_3_q));  // open: clr
  Byte_MUX byte_mux_3 (
    .select_input(or_2_out), .in_0(byte_mux_2_out_4), .in_1(byte_mux_4_out_4), .out_4(byte_mux_3_out_4));
  MUX_4_Byte mux_4_byte_1 (
    .Adress_bus_in(byte_switch_3_o), .in_2(reg_0_q), .in_3(reg_1_q), .in_4(reg_2_q), .in_5(reg_3_q),
    .out_6(out_6));
  MUX_4_Byte mux_4_byte_2 (
    .Adress_bus_in(byte_switch_3_o), .in_2(reg_0_q), .in_3(reg_1_q), .in_4(reg_2_q), .in_5(reg_3_q),
    .out_6(mux_4_byte_2_out_6));
  alu_decoder Instruction_decoder (
    .instruction_Bus_in(byte_switch_2_o), .subtraction(Instruction_decoder_subtraction),
    .addition(Instruction_decoder_addition));
  Byte_switch byte_switch_4 (.i(reg_1_q), .switch(Instruction_decoder_subtraction), .o(byte_switch_4_o));
  Byte_switch byte_switch_5 (.i(reg_2_q), .switch(Instruction_decoder_subtraction), .o(byte_switch_5_o));
  Byte_switch byte_switch_6 (.i(reg_1_q), .switch(Instruction_decoder_addition), .o(byte_switch_6_o));
  Byter_adder addition (.i_1(byte_switch_6_o), .i_2(byte_switch_7_o), .o_1(out_8), .carry(out_9));
  Byte_switch byte_switch_7 (.i(reg_2_q), .switch(Instruction_decoder_addition), .o(byte_switch_7_o));
  or or_2 (or_2_out, Instruction_decoder_addition, Instruction_decoder_subtraction);
  Byte_inverter byte_inverter_1 (.in_1(byte_switch_5_o), .out_2(byte_inverter_1_out_2));
  Byte_MUX byte_mux_4 (
    .select_input(Instruction_decoder_addition), .in_0(out_7), .in_1(out_8), .out_4(byte_mux_4_out_4));
  Byter_adder subtraction (.i_1(byte_switch_4_o), .i_2(byter_adder_1_o_1), .o_1(out_7));  // open: carry
  Byter_adder byter_adder_1 (.i_1(byte_inverter_1_out_2), .i_2(8'h1), .o_1(byter_adder_1_o_1));  // open: carry

  // Notes on the sheet:
  //   write
  //   |
  //   read
  //   Data Bus
  //   Instruction Bus
  //   Adress Bus
  //   input selecter
endmodule

module full_adder (
  input  A,
  input  B,
  input  C_in_6a097d25,
  output sum,
  output count
);

  wire and_1_out, and_2_out, xor_1_out;

  xor xor_1 (xor_1_out, A, B);
  and and_1 (and_1_out, A, B);
  xor xor_2 (sum, xor_1_out, C_in_6a097d25);
  and and_2 (and_2_out, xor_1_out, C_in_6a097d25);
  or or_1 (count, and_2_out, and_1_out);
endmodule

module Gated_Latch (
  input  set,
  input  reset,
  output out_3
);

  wire and_1_out, and_2_out, not_1_out, not_2_out, or_1_out;

  not not_1 (not_1_out, set);
  and and_1 (and_1_out, set, reset);
  and and_2 (and_2_out, not_1_out, reset);
  or or_1 (or_1_out, out_3, and_1_out);
  not not_2 (not_2_out, and_2_out);
  and and_3 (out_3, or_1_out, not_2_out);
endmodule

module Byte_register (
  input  clock_in,
  input  enable_write,
  input  [7:0] data_in,
  output [7:0] data_out
);

  wire and_1_out, and_2_out, and_3_out, and_4_out, and_5_out, and_6_out, and_7_out, and_8_out, and_9_out,
       and_10_out, and_11_out, and_12_out, and_13_out, and_14_out, and_15_out, and_16_out, and_17_out,
       not_1_out, not_2_out, not_3_out, not_4_out, not_5_out, not_6_out, not_7_out, not_8_out, not_9_out,
       not_10_out, not_11_out, not_12_out, not_13_out, not_14_out, not_15_out, not_16_out, or_1_out,
       or_2_out, or_3_out, or_4_out, or_5_out, or_6_out, or_7_out, or_8_out;

  and and_1 (and_1_out, enable_write, clock_in);
  not not_1 (not_1_out, data_in[0]);
  not not_2 (not_2_out, data_in[1]);
  not not_3 (not_3_out, data_in[2]);
  not not_4 (not_4_out, data_in[3]);
  not not_5 (not_5_out, data_in[4]);
  not not_6 (not_6_out, data_in[5]);
  not not_7 (not_7_out, data_in[6]);
  not not_8 (not_8_out, data_in[7]);
  and and_2 (and_2_out, data_in[0], and_1_out);
  and and_3 (and_3_out, not_1_out, and_1_out);
  and and_4 (and_4_out, data_in[1], and_1_out);
  and and_5 (and_5_out, not_2_out, and_1_out);
  and and_6 (and_6_out, data_in[2], and_1_out);
  and and_7 (and_7_out, not_3_out, and_1_out);
  and and_8 (and_8_out, data_in[3], and_1_out);
  and and_9 (and_9_out, not_4_out, and_1_out);
  and and_10 (and_10_out, data_in[4], and_1_out);
  and and_11 (and_11_out, not_5_out, and_1_out);
  and and_12 (and_12_out, data_in[5], and_1_out);
  and and_13 (and_13_out, not_6_out, and_1_out);
  and and_14 (and_14_out, data_in[6], and_1_out);
  and and_15 (and_15_out, not_7_out, and_1_out);
  and and_16 (and_16_out, data_in[7], and_1_out);
  and and_17 (and_17_out, not_8_out, and_1_out);
  or or_1 (or_1_out, data_out[0], and_2_out);
  not not_9 (not_9_out, and_3_out);
  or or_2 (or_2_out, data_out[1], and_4_out);
  not not_10 (not_10_out, and_5_out);
  or or_3 (or_3_out, data_out[2], and_6_out);
  not not_11 (not_11_out, and_7_out);
  or or_4 (or_4_out, data_out[3], and_8_out);
  not not_12 (not_12_out, and_9_out);
  or or_5 (or_5_out, data_out[4], and_10_out);
  not not_13 (not_13_out, and_11_out);
  or or_6 (or_6_out, data_out[5], and_12_out);
  not not_14 (not_14_out, and_13_out);
  or or_7 (or_7_out, data_out[6], and_14_out);
  not not_15 (not_15_out, and_15_out);
  or or_8 (or_8_out, data_out[7], and_16_out);
  not not_16 (not_16_out, and_17_out);
  and and_18 (data_out[0], or_1_out, not_9_out);
  and and_19 (data_out[1], or_2_out, not_10_out);
  and and_20 (data_out[2], or_3_out, not_11_out);
  and and_21 (data_out[3], or_4_out, not_12_out);
  and and_22 (data_out[4], or_5_out, not_13_out);
  and and_23 (data_out[5], or_6_out, not_14_out);
  and and_24 (data_out[6], or_7_out, not_15_out);
  and and_25 (data_out[7], or_8_out, not_16_out);
endmodule

module decoder_2_bit (
  input  in_1_2c4f912e,
  input  in_2_2398e526,
  output out_1_367624e9,
  output out_2_0610cceb,
  output out_3_f383ddb4,
  output out_4_fdb79afc
);

  wire not_1_out, not_2_out;

  not not_1 (not_1_out, in_1_2c4f912e);
  not not_2 (not_2_out, in_2_2398e526);
  nor nor_1 (out_1_367624e9, in_1_2c4f912e, in_2_2398e526);
  and and_1 (out_2_0610cceb, not_1_out, in_2_2398e526);
  and and_2 (out_3_f383ddb4, in_1_2c4f912e, not_2_out);
  and and_3 (out_4_fdb79afc, in_1_2c4f912e, in_2_2398e526);
endmodule

module adress_memory_16_bit (
  input  write_1,
  input  write_2,
  input  write_3,
  input  write_4,
  input  read_1,
  input  read_2,
  input  read_3,
  input  read_4,
  input  enable_read,
  input  enable_write,
  input  input_value,
  output output_value
);

  wire and_1_out, and_2_out, and_3_out, and_4_out, and_5_out, and_6_out, and_7_out, and_8_out, and_9_out,
       and_10_out, and_11_out, and_12_out, and_13_out, and_14_out, and_15_out, and_16_out, and_17_out,
       and_18_out, and_19_out, and_20_out, and_21_out, and_22_out, and_23_out, and_24_out, and_25_out,
       and_26_out, and_27_out, and_28_out, and_29_out, and_30_out, and_31_out, and_32_out, and_33_out,
       and_34_out, and_35_out, and_36_out, and_37_out, and_38_out, and_39_out, and_40_out, and_41_out,
       and_42_out, and_43_out, and_44_out, and_45_out, and_46_out, and_47_out, and_48_out, and_49_out,
       and_50_out, and_51_out, and_52_out, and_53_out, and_54_out, and_55_out, and_56_out, and_57_out,
       and_58_out, and_59_out, and_60_out, and_61_out, and_62_out, and_63_out, and_64_out, and_65_out,
       and_66_out, and_67_out, and_68_out, and_69_out, and_70_out, and_71_out, and_72_out, and_73_out,
       and_74_out, and_75_out, and_76_out, and_77_out, and_78_out, and_79_out, and_80_out,
       decoder_2_bit_1_out_1_367624e9, decoder_2_bit_1_out_2_0610cceb, decoder_2_bit_1_out_3_f383ddb4,
       decoder_2_bit_1_out_4_fdb79afc, decoder_2_bit_2_out_1_367624e9, decoder_2_bit_2_out_2_0610cceb,
       decoder_2_bit_2_out_3_f383ddb4, decoder_2_bit_2_out_4_fdb79afc, decoder_2_bit_3_out_1_367624e9,
       decoder_2_bit_3_out_2_0610cceb, decoder_2_bit_3_out_3_f383ddb4, decoder_2_bit_3_out_4_fdb79afc,
       decoder_2_bit_4_out_1_367624e9, decoder_2_bit_4_out_2_0610cceb, decoder_2_bit_4_out_3_f383ddb4,
       decoder_2_bit_4_out_4_fdb79afc, gated_latch_1_out_3, gated_latch_2_out_3, gated_latch_3_out_3,
       gated_latch_4_out_3, gated_latch_5_out_3, gated_latch_6_out_3, gated_latch_7_out_3,
       gated_latch_8_out_3, gated_latch_9_out_3, gated_latch_10_out_3, gated_latch_11_out_3,
       gated_latch_12_out_3, gated_latch_13_out_3, gated_latch_14_out_3, gated_latch_15_out_3,
       gated_latch_16_out_3, or_1_out, or_2_out, or_3_out, or_4_out, or_5_out, or_6_out, or_7_out, or_8_out,
       or_9_out, or_10_out, or_11_out, or_12_out, or_13_out, or_14_out, or_15_out, or_16_out, or_17_out,
       or_18_out, or_19_out, or_20_out, or_21_out, or_22_out;

  decoder_2_bit decoder_2_bit_1 (
    .in_1_2c4f912e(write_1), .in_2_2398e526(write_2), .out_1_367624e9(decoder_2_bit_1_out_1_367624e9),
    .out_2_0610cceb(decoder_2_bit_1_out_2_0610cceb), .out_3_f383ddb4(decoder_2_bit_1_out_3_f383ddb4),
    .out_4_fdb79afc(decoder_2_bit_1_out_4_fdb79afc));
  decoder_2_bit decoder_2_bit_2 (
    .in_1_2c4f912e(write_3), .in_2_2398e526(write_4), .out_1_367624e9(decoder_2_bit_2_out_1_367624e9),
    .out_2_0610cceb(decoder_2_bit_2_out_2_0610cceb), .out_3_f383ddb4(decoder_2_bit_2_out_3_f383ddb4),
    .out_4_fdb79afc(decoder_2_bit_2_out_4_fdb79afc));
  decoder_2_bit decoder_2_bit_3 (
    .in_1_2c4f912e(read_1), .in_2_2398e526(read_2), .out_1_367624e9(decoder_2_bit_3_out_1_367624e9),
    .out_2_0610cceb(decoder_2_bit_3_out_2_0610cceb), .out_3_f383ddb4(decoder_2_bit_3_out_3_f383ddb4),
    .out_4_fdb79afc(decoder_2_bit_3_out_4_fdb79afc));
  decoder_2_bit decoder_2_bit_4 (
    .in_1_2c4f912e(read_3), .in_2_2398e526(read_4), .out_1_367624e9(decoder_2_bit_4_out_1_367624e9),
    .out_2_0610cceb(decoder_2_bit_4_out_2_0610cceb), .out_3_f383ddb4(decoder_2_bit_4_out_3_f383ddb4),
    .out_4_fdb79afc(decoder_2_bit_4_out_4_fdb79afc));
  LED led_1 (.in(enable_read));
  LED led_2 (.in(enable_write));
  LED led_3 (.in(input_value));
  and and_1 (and_1_out, decoder_2_bit_2_out_1_367624e9, enable_write);
  and and_2 (and_2_out, decoder_2_bit_4_out_1_367624e9, enable_read);
  and and_3 (and_3_out, decoder_2_bit_2_out_2_0610cceb, enable_write);
  and and_4 (and_4_out, decoder_2_bit_4_out_2_0610cceb, enable_read);
  and and_5 (and_5_out, decoder_2_bit_2_out_3_f383ddb4, enable_write);
  and and_6 (and_6_out, decoder_2_bit_4_out_3_f383ddb4, enable_read);
  and and_7 (and_7_out, decoder_2_bit_2_out_4_fdb79afc, enable_write);
  and and_8 (and_8_out, decoder_2_bit_4_out_4_fdb79afc, enable_read);
  and and_9 (and_9_out, enable_read, decoder_2_bit_3_out_4_fdb79afc);
  or or_1 (or_1_out, and_1_out, and_2_out);
  or or_2 (or_2_out, and_3_out, and_4_out);
  or or_3 (or_3_out, and_5_out, and_6_out);
  or or_4 (or_4_out, and_7_out, and_8_out);
  and and_10 (and_10_out, enable_write, decoder_2_bit_1_out_4_fdb79afc);
  or or_5 (or_5_out, and_9_out, and_10_out);
  and and_11 (and_11_out, or_5_out, or_1_out);
  LED led_4 (.in(and_11_out));
  and and_12 (and_12_out, and_11_out, enable_read);
  and and_13 (and_13_out, and_11_out, enable_write);
  and and_14 (and_14_out, or_5_out, or_2_out);
  LED led_5 (.in(and_14_out));
  and and_15 (and_15_out, and_14_out, enable_read);
  and and_16 (and_16_out, and_14_out, enable_write);
  and and_17 (and_17_out, or_5_out, or_3_out);
  LED led_6 (.in(and_17_out));
  and and_18 (and_18_out, and_17_out, enable_read);
  and and_19 (and_19_out, and_17_out, enable_write);
  and and_20 (and_20_out, or_5_out, or_4_out);
  LED led_7 (.in(and_20_out));
  and and_21 (and_21_out, and_20_out, enable_read);
  and and_22 (and_22_out, and_20_out, enable_write);
  and and_23 (and_23_out, and_12_out, gated_latch_1_out_3);
  LED led_8 (.in(gated_latch_1_out_3));
  Gated_Latch gated_latch_1 (.set(input_value), .reset(and_13_out), .out_3(gated_latch_1_out_3));
  or or_6 (or_6_out, and_24_out, and_23_out);
  and and_24 (and_24_out, and_15_out, gated_latch_2_out_3);
  LED led_9 (.in(gated_latch_2_out_3));
  Gated_Latch gated_latch_2 (.set(input_value), .reset(and_16_out), .out_3(gated_latch_2_out_3));
  or or_7 (or_7_out, and_25_out, or_6_out);
  and and_25 (and_25_out, and_18_out, gated_latch_3_out_3);
  LED led_10 (.in(gated_latch_3_out_3));
  Gated_Latch gated_latch_3 (.set(input_value), .reset(and_19_out), .out_3(gated_latch_3_out_3));
  or or_8 (or_8_out, and_26_out, or_7_out);
  and and_26 (and_26_out, and_21_out, gated_latch_4_out_3);
  LED led_11 (.in(gated_latch_4_out_3));
  Gated_Latch gated_latch_4 (.set(input_value), .reset(and_22_out), .out_3(gated_latch_4_out_3));
  and and_27 (and_27_out, enable_read, decoder_2_bit_3_out_3_f383ddb4);
  or or_9 (or_9_out, and_27_out, and_28_out);
  and and_28 (and_28_out, enable_write, decoder_2_bit_1_out_3_f383ddb4);
  and and_29 (and_29_out, or_9_out, or_1_out);
  LED led_12 (.in(and_29_out));
  and and_30 (and_30_out, and_29_out, enable_read);
  and and_31 (and_31_out, and_29_out, enable_write);
  Gated_Latch gated_latch_5 (.set(input_value), .reset(and_31_out), .out_3(gated_latch_5_out_3));
  and and_32 (and_32_out, or_9_out, or_2_out);
  LED led_13 (.in(and_32_out));
  and and_33 (and_33_out, and_32_out, enable_read);
  and and_34 (and_34_out, and_32_out, enable_write);
  Gated_Latch gated_latch_6 (.set(input_value), .reset(and_34_out), .out_3(gated_latch_6_out_3));
  and and_35 (and_35_out, or_9_out, or_3_out);
  LED led_14 (.in(and_35_out));
  and and_36 (and_36_out, and_35_out, enable_read);
  and and_37 (and_37_out, and_35_out, enable_write);
  Gated_Latch gated_latch_7 (.set(input_value), .reset(and_37_out), .out_3(gated_latch_7_out_3));
  and and_38 (and_38_out, or_9_out, or_4_out);
  LED led_15 (.in(and_38_out));
  and and_39 (and_39_out, and_38_out, enable_read);
  and and_40 (and_40_out, and_38_out, enable_write);
  Gated_Latch gated_latch_8 (.set(input_value), .reset(and_40_out), .out_3(gated_latch_8_out_3));
  and and_41 (and_41_out, enable_read, decoder_2_bit_3_out_2_0610cceb);
  and and_42 (and_42_out, and_30_out, gated_latch_5_out_3);
  LED led_16 (.in(gated_latch_5_out_3));
  or or_10 (or_10_out, and_43_out, and_42_out);
  and and_43 (and_43_out, and_33_out, gated_latch_6_out_3);
  LED led_17 (.in(gated_latch_6_out_3));
  or or_11 (or_11_out, and_44_out, or_10_out);
  and and_44 (and_44_out, and_36_out, gated_latch_7_out_3);
  LED led_18 (.in(gated_latch_7_out_3));
  or or_12 (or_12_out, and_45_out, or_11_out);
  and and_45 (and_45_out, and_39_out, gated_latch_8_out_3);
  LED led_19 (.in(gated_latch_8_out_3));
  and and_46 (and_46_out, enable_write, decoder_2_bit_1_out_2_0610cceb);
  or or_13 (or_13_out, and_41_out, and_46_out);
  or or_14 (or_14_out, or_12_out, or_8_out);
  and and_47 (and_47_out, or_13_out, or_1_out);
  LED led_20 (.in(and_47_out));
  and and_48 (and_48_out, and_47_out, enable_read);
  and and_49 (and_49_out, and_47_out, enable_write);
  and and_50 (and_50_out, or_13_out, or_2_out);
  LED led_21 (.in(and_50_out));
  and and_51 (and_51_out, and_50_out, enable_read);
  and and_52 (and_52_out, and_50_out, enable_write);
  and and_53 (and_53_out, or_13_out, or_3_out);
  LED led_22 (.in(and_53_out));
  and and_54 (and_54_out, and_53_out, enable_read);
  and and_55 (and_55_out, and_53_out, enable_write);
  and and_56 (and_56_out, or_13_out, or_4_out);
  LED led_23 (.in(and_56_out));
  and and_57 (and_57_out, and_56_out, enable_read);
  and and_58 (and_58_out, and_56_out, enable_write);
  and and_59 (and_59_out, and_48_out, gated_latch_9_out_3);
  LED led_24 (.in(gated_latch_9_out_3));
  Gated_Latch gated_latch_9 (.set(input_value), .reset(and_49_out), .out_3(gated_latch_9_out_3));
  and and_60 (and_60_out, and_51_out, gated_latch_10_out_3);
  LED led_25 (.in(gated_latch_10_out_3));
  Gated_Latch gated_latch_10 (.set(input_value), .reset(and_52_out), .out_3(gated_latch_10_out_3));
  and and_61 (and_61_out, and_54_out, gated_latch_11_out_3);
  LED led_26 (.in(gated_latch_11_out_3));
  Gated_Latch gated_latch_11 (.set(input_value), .reset(and_55_out), .out_3(gated_latch_11_out_3));
  and and_62 (and_62_out, and_57_out, gated_latch_12_out_3);
  LED led_27 (.in(gated_latch_12_out_3));
  Gated_Latch gated_latch_12 (.set(input_value), .reset(and_58_out), .out_3(gated_latch_12_out_3));
  and and_63 (and_63_out, enable_read, decoder_2_bit_3_out_1_367624e9);
  or or_15 (or_15_out, and_63_out, and_64_out);
  or or_16 (or_16_out, and_60_out, and_59_out);
  or or_17 (or_17_out, and_61_out, or_16_out);
  or or_18 (or_18_out, and_62_out, or_17_out);
  or or_19 (or_19_out, or_18_out, or_14_out);
  and and_64 (and_64_out, enable_write, decoder_2_bit_1_out_1_367624e9);
  and and_65 (and_65_out, or_15_out, or_1_out);
  LED led_28 (.in(and_65_out));
  and and_66 (and_66_out, and_65_out, enable_read);
  and and_67 (and_67_out, and_65_out, enable_write);
  and and_68 (and_68_out, or_15_out, or_2_out);
  LED led_29 (.in(and_68_out));
  and and_69 (and_69_out, and_68_out, enable_read);
  and and_70 (and_70_out, and_68_out, enable_write);
  and and_71 (and_71_out, or_15_out, or_3_out);
  LED led_30 (.in(and_71_out));
  and and_72 (and_72_out, and_71_out, enable_read);
  and and_73 (and_73_out, and_71_out, enable_write);
  and and_74 (and_74_out, or_15_out, or_4_out);
  LED led_31 (.in(and_74_out));
  and and_75 (and_75_out, and_74_out, enable_read);
  and and_76 (and_76_out, and_74_out, enable_write);
  and and_77 (and_77_out, and_66_out, gated_latch_13_out_3);
  LED led_32 (.in(gated_latch_13_out_3));
  Gated_Latch gated_latch_13 (.set(input_value), .reset(and_67_out), .out_3(gated_latch_13_out_3));
  or or_20 (or_20_out, and_78_out, and_77_out);
  and and_78 (and_78_out, and_69_out, gated_latch_14_out_3);
  LED led_33 (.in(gated_latch_14_out_3));
  Gated_Latch gated_latch_14 (.set(input_value), .reset(and_70_out), .out_3(gated_latch_14_out_3));
  or or_21 (or_21_out, and_79_out, or_20_out);
  and and_79 (and_79_out, and_72_out, gated_latch_15_out_3);
  LED led_34 (.in(gated_latch_15_out_3));
  Gated_Latch gated_latch_15 (.set(input_value), .reset(and_73_out), .out_3(gated_latch_15_out_3));
  or or_22 (or_22_out, and_80_out, or_21_out);
  and and_80 (and_80_out, and_75_out, gated_latch_16_out_3);
  LED led_35 (.in(gated_latch_16_out_3));
  Gated_Latch gated_latch_16 (.set(input_value), .reset(and_76_out), .out_3(gated_latch_16_out_3));
  or or_23 (output_value, or_22_out, or_19_out);
  LED led_36 (.in(output_value));
endmodule

module adress_memory_16_x_1_byte (
  input  bit_1_1,
  input  bit_2_2,
  input  bit_3_4,
  input  bit_4_8,
  input  bit_5_16,
  input  bit_6_32,
  input  bit_7_64,
  input  bit_8_128,
  input  a_1,
  input  a_2,
  input  a_3,
  input  a_4,
  input  enable_read,
  input  enable_write,
  output out_1_1,
  output out_2_2,
  output out_3_4,
  output out_4_8,
  output out_5_16,
  output out_6_32,
  output out_7_64,
  output out_8_128
);

  adress_memory_16_bit adress_memory_16_bit_1 (
    .write_1(a_1), .write_2(a_2), .write_3(a_3), .write_4(a_4), .read_1(enable_read), .read_2(enable_write),
    .read_3(bit_1_1), .enable_write(a_1), .input_value(a_2), .output_value(out_8_128));  // open: read_4, enable_read
  adress_memory_16_bit adress_memory_16_bit_2 (
    .write_1(a_1), .write_2(a_2), .write_3(a_3), .write_4(a_4), .read_1(enable_read), .read_2(enable_write),
    .read_3(bit_2_2), .enable_write(a_1), .input_value(a_2), .output_value(out_7_64));  // open: read_4, enable_read
  adress_memory_16_bit adress_memory_16_bit_3 (
    .write_1(a_1), .write_2(a_2), .write_3(a_3), .write_4(a_4), .read_1(enable_read), .read_2(enable_write),
    .read_3(bit_3_4), .enable_write(a_1), .input_value(a_2), .output_value(out_6_32));  // open: read_4, enable_read
  adress_memory_16_bit adress_memory_16_bit_4 (
    .write_1(a_1), .write_2(a_2), .write_3(a_3), .write_4(a_4), .read_1(enable_read), .read_2(enable_write),
    .read_3(bit_4_8), .enable_write(a_1), .input_value(a_2), .output_value(out_5_16));  // open: read_4, enable_read
  adress_memory_16_bit adress_memory_16_bit_5 (
    .write_1(a_1), .write_2(a_2), .write_3(a_3), .write_4(a_4), .read_1(enable_read), .read_2(enable_write),
    .read_3(bit_5_16), .enable_write(a_1), .input_value(a_2), .output_value(out_4_8));  // open: read_4, enable_read
  adress_memory_16_bit adress_memory_16_bit_6 (
    .write_1(a_1), .write_2(a_2), .write_3(a_3), .write_4(a_4), .read_1(enable_read), .read_2(enable_write),
    .read_3(bit_6_32), .enable_write(a_1), .input_value(a_2), .output_value(out_3_4));  // open: read_4, enable_read
  adress_memory_16_bit adress_memory_16_bit_7 (
    .write_1(a_1), .write_2(a_2), .write_3(a_3), .write_4(a_4), .read_1(enable_read), .read_2(enable_write),
    .read_3(bit_7_64), .enable_write(a_1), .input_value(a_2), .output_value(out_2_2));  // open: read_4, enable_read
  adress_memory_16_bit adress_memory_16_bit_8 (
    .write_1(a_1), .write_2(a_2), .write_3(a_3), .write_4(a_4), .read_1(enable_read), .read_2(enable_write),
    .read_3(bit_8_128), .output_value(out_1_1));  // open: read_4, enable_read, enable_write, input_value

  // Notes on the sheet:
  //   Data_Bus
  //   Adress_Bus
endmodule

module memory_cell_1_bit (
  input  data_in,
  input  enable_write,
  output data_out
);

  wire and_1_out, and_2_out, not_1_out, not_2_out, or_1_out;

  not not_1 (not_1_out, data_in);
  and and_1 (and_1_out, data_in, enable_write);
  and and_2 (and_2_out, not_1_out, enable_write);
  not not_2 (not_2_out, and_2_out);
  or or_1 (or_1_out, data_out, and_1_out);
  and and_3 (data_out, or_1_out, not_2_out);
endmodule

module adress_memory_8_byte (
);

  Byte_register byte_register_1 ();  // open: data_in, enable_write, clock_in, data_out
  Byte_register byte_register_2 ();  // open: data_in, enable_write, clock_in, data_out
endmodule

module adress_memory_write_tp_self (
  input  write_adress_1,
  input  write_adress_2,
  input  write_adress_3,
  input  write_adress_4,
  input  read_adress_1,
  input  read_adress_2,
  input  read_adress_3,
  input  read_adress_4,
  input  enable_read,
  input  enable_write,
  input  switch_input,
  input  data_in_1,
  input  data_in_2,
  input  data_in_3,
  input  data_in_4,
  input  data_in_5,
  input  data_in_6,
  input  data_in_7,
  input  data_in_8,
  output out_20,
  output out_21,
  output out_22,
  output out_23,
  output out_24,
  output out_25,
  output out_26,
  output out_27
);

  wire mux_1_out_4, mux_2_out_4, mux_3_out_4, mux_4_out_4, mux_5_out_4, mux_6_out_4, mux_7_out_4, mux_8_out_4;

  MUX mux_1 (.in_2(out_20), .in_3(data_in_1), .in_1(switch_input), .out_4(mux_1_out_4));
  MUX mux_2 (.in_2(out_21), .in_3(data_in_2), .in_1(switch_input), .out_4(mux_2_out_4));
  MUX mux_3 (.in_2(out_22), .in_3(data_in_3), .in_1(switch_input), .out_4(mux_3_out_4));
  MUX mux_4 (.in_2(out_23), .in_3(data_in_4), .in_1(switch_input), .out_4(mux_4_out_4));
  MUX mux_5 (.in_2(out_24), .in_3(data_in_5), .in_1(switch_input), .out_4(mux_5_out_4));
  MUX mux_6 (.in_2(out_25), .in_3(data_in_6), .in_1(switch_input), .out_4(mux_6_out_4));
  MUX mux_7 (.in_2(out_26), .in_3(data_in_7), .in_1(switch_input), .out_4(mux_7_out_4));
  MUX mux_8 (.in_2(out_27), .in_3(data_in_8), .in_1(switch_input), .out_4(mux_8_out_4));
  adress_memory_16_bit adress_memory_16_bit_1 (
    .write_1(write_adress_1), .write_2(write_adress_2), .write_3(write_adress_3), .write_4(write_adress_4),
    .read_1(read_adress_1), .read_2(read_adress_2), .read_3(read_adress_3), .read_4(read_adress_4),
    .enable_read(enable_read), .enable_write(enable_write), .input_value(mux_1_out_4), .output_value(out_20));
  adress_memory_16_bit adress_memory_16_bit_2 (
    .write_1(write_adress_1), .write_2(write_adress_2), .write_3(write_adress_3), .write_4(write_adress_4),
    .read_1(read_adress_1), .read_2(read_adress_2), .read_3(read_adress_3), .read_4(read_adress_4),
    .enable_read(enable_read), .enable_write(enable_write), .input_value(mux_2_out_4), .output_value(out_21));
  adress_memory_16_bit adress_memory_16_bit_3 (
    .write_1(write_adress_1), .write_2(write_adress_2), .write_3(write_adress_3), .write_4(write_adress_4),
    .read_1(read_adress_1), .read_2(read_adress_2), .read_3(read_adress_3), .read_4(read_adress_4),
    .enable_read(enable_read), .enable_write(enable_write), .input_value(mux_3_out_4), .output_value(out_22));
  adress_memory_16_bit adress_memory_16_bit_4 (
    .write_1(write_adress_1), .write_2(write_adress_2), .write_3(write_adress_3), .write_4(write_adress_4),
    .read_1(read_adress_1), .read_2(read_adress_2), .read_3(read_adress_3), .read_4(read_adress_4),
    .enable_read(enable_read), .enable_write(enable_write), .input_value(mux_4_out_4), .output_value(out_23));
  adress_memory_16_bit adress_memory_16_bit_5 (
    .write_1(write_adress_1), .write_2(write_adress_2), .write_3(write_adress_3), .write_4(write_adress_4),
    .read_1(read_adress_1), .read_2(read_adress_2), .read_3(read_adress_3), .read_4(read_adress_4),
    .enable_read(enable_read), .enable_write(enable_write), .input_value(mux_5_out_4), .output_value(out_24));
  adress_memory_16_bit adress_memory_16_bit_6 (
    .write_1(write_adress_1), .write_2(write_adress_2), .write_3(write_adress_3), .write_4(write_adress_4),
    .read_1(read_adress_1), .read_2(read_adress_2), .read_3(read_adress_3), .read_4(read_adress_4),
    .enable_read(enable_read), .enable_write(enable_write), .input_value(mux_6_out_4), .output_value(out_25));
  adress_memory_16_bit adress_memory_16_bit_7 (
    .write_1(write_adress_1), .write_2(write_adress_2), .write_3(write_adress_3), .write_4(write_adress_4),
    .read_1(read_adress_1), .read_2(read_adress_2), .read_3(read_adress_3), .read_4(read_adress_4),
    .enable_read(enable_read), .enable_write(enable_write), .input_value(mux_7_out_4), .output_value(out_26));
  adress_memory_16_bit adress_memory_16_bit_8 (
    .write_1(write_adress_1), .write_2(write_adress_2), .write_3(write_adress_3), .write_4(write_adress_4),
    .read_1(read_adress_1), .read_2(read_adress_2), .read_3(read_adress_3), .read_4(read_adress_4),
    .enable_read(enable_read), .enable_write(enable_write), .input_value(mux_8_out_4), .output_value(out_27));
endmodule

module MUX (
  input  in_1,
  input  in_2,
  input  in_3,
  output out_4
);

  wire and_1_out, and_2_out, not_1_out;

  not not_1 (not_1_out, in_1);
  and and_1 (and_1_out, not_1_out, in_2);
  and and_2 (and_2_out, in_1, in_3);
  or or_1 (out_4, and_1_out, and_2_out);
endmodule

module Byte_MUX (
  input  select_input,
  input  [7:0] in_0,
  input  [7:0] in_1,
  output [7:0] out_4
);

  MUX mux_1 (.in_2(in_0[0]), .in_3(in_1[0]), .in_1(select_input), .out_4(out_4[0]));
  MUX mux_2 (.in_2(in_0[1]), .in_3(in_1[1]), .in_1(select_input), .out_4(out_4[1]));
  MUX mux_3 (.in_2(in_0[2]), .in_3(in_1[2]), .in_1(select_input), .out_4(out_4[2]));
  MUX mux_4 (.in_2(in_0[3]), .in_3(in_1[3]), .in_1(select_input), .out_4(out_4[3]));
  MUX mux_5 (.in_2(in_0[4]), .in_3(in_1[4]), .in_1(select_input), .out_4(out_4[4]));
  MUX mux_6 (.in_2(in_0[5]), .in_3(in_1[5]), .in_1(select_input), .out_4(out_4[5]));
  MUX mux_7 (.in_2(in_0[6]), .in_3(in_1[6]), .in_1(select_input), .out_4(out_4[6]));
  MUX mux_8 (.in_2(in_0[7]), .in_3(in_1[7]), .in_1(select_input), .out_4(out_4[7]));
endmodule

module Byter_adder (
  input  [7:0] i_1,
  input  [7:0] i_2,
  output [7:0] o_1,
  output carry
);

  wire full_adder_1_count, full_adder_2_count, full_adder_3_count, full_adder_4_count, full_adder_5_count,
       full_adder_6_count, full_adder_7_count;

  full_adder full_adder_1 (.A(i_2[0]), .B(i_1[0]), .sum(o_1[0]), .count(full_adder_1_count));  // open: C_in_6a097d25
  full_adder full_adder_2 (
    .A(full_adder_1_count), .B(i_1[1]), .C_in_6a097d25(i_2[1]), .sum(o_1[1]), .count(full_adder_2_count));
  full_adder full_adder_3 (
    .A(full_adder_2_count), .B(i_1[2]), .C_in_6a097d25(i_2[2]), .sum(o_1[2]), .count(full_adder_3_count));
  full_adder full_adder_4 (
    .A(full_adder_3_count), .B(i_1[3]), .C_in_6a097d25(i_2[3]), .sum(o_1[3]), .count(full_adder_4_count));
  full_adder full_adder_5 (
    .A(full_adder_4_count), .B(i_1[4]), .C_in_6a097d25(i_2[4]), .sum(o_1[4]), .count(full_adder_5_count));
  full_adder full_adder_6 (
    .A(full_adder_5_count), .B(i_1[5]), .C_in_6a097d25(i_2[5]), .sum(o_1[5]), .count(full_adder_6_count));
  full_adder full_adder_7 (
    .A(full_adder_6_count), .B(i_1[6]), .C_in_6a097d25(i_2[6]), .sum(o_1[6]), .count(full_adder_7_count));
  full_adder full_adder_8 (.A(full_adder_7_count), .B(i_1[7]), .C_in_6a097d25(i_2[7]), .sum(o_1[7]), .count(carry));
endmodule

module Byte_inverter (
  input  [7:0] in_1,
  output [7:0] out_2
);

  not not_1 (out_2[0], in_1[0]);
  not not_2 (out_2[1], in_1[1]);
  not not_3 (out_2[2], in_1[2]);
  not not_4 (out_2[3], in_1[3]);
  not not_5 (out_2[4], in_1[4]);
  not not_6 (out_2[5], in_1[5]);
  not not_7 (out_2[6], in_1[6]);
  not not_8 (out_2[7], in_1[7]);
endmodule

module Byte_switch (
  input  switch,
  input  [7:0] i,
  output [7:0] o
);

  and and_1 (o[0], i[0], switch);
  and and_2 (o[1], i[1], switch);
  and and_3 (o[2], i[2], switch);
  and and_4 (o[3], i[3], switch);
  and and_5 (o[4], i[4], switch);
  and and_6 (o[5], i[5], switch);
  and and_7 (o[6], i[6], switch);
  and and_8 (o[7], i[7], switch);
endmodule

module MUX_4_Byte (
  input  [7:0] Adress_bus_in,
  input  [7:0] in_2,
  input  [7:0] in_3,
  input  [7:0] in_4,
  input  [7:0] in_5,
  output [7:0] out_6
);

  wire or_1_out, tmp_1_adress_0, tmp_1_adress_1, tmp_1_adress_2, tmp_1_adress_3;
  wire [7:0] byte_mux_1_out_4, byte_mux_2_out_4, byte_switch_1_o, byte_switch_2_o, byte_switch_3_o,
       byte_switch_4_o;

  tmp tmp_1 (
    .adress_bus_in(Adress_bus_in), .adress_0(tmp_1_adress_0), .adress_1(tmp_1_adress_1),
    .adress_2(tmp_1_adress_2), .adress_3(tmp_1_adress_3));
  Byte_switch byte_switch_1 (.i(in_2), .switch(tmp_1_adress_0), .o(byte_switch_1_o));
  Byte_switch byte_switch_2 (.i(in_3), .switch(tmp_1_adress_1), .o(byte_switch_2_o));
  Byte_switch byte_switch_3 (.i(in_4), .switch(tmp_1_adress_2), .o(byte_switch_3_o));
  Byte_switch byte_switch_4 (.i(in_5), .switch(tmp_1_adress_3), .o(byte_switch_4_o));
  or or_1 (or_1_out, tmp_1_adress_2, tmp_1_adress_3);
  Byte_MUX byte_mux_1 (
    .select_input(tmp_1_adress_1), .in_0(byte_switch_1_o), .in_1(byte_switch_2_o), .out_4(byte_mux_1_out_4));
  Byte_MUX byte_mux_2 (
    .select_input(tmp_1_adress_3), .in_0(byte_switch_3_o), .in_1(byte_switch_4_o), .out_4(byte_mux_2_out_4));
  Byte_MUX byte_mux_3 (.select_input(or_1_out), .in_0(byte_mux_1_out_4), .in_1(byte_mux_2_out_4), .out_4(out_6));
endmodule

module Byte_decoder (
  input  [7:0] adress_bus_in,
  output adress_0,
  output adress_1,
  output adress_2,
  output adress_3
);

  wire and_1_out, and_2_out, and_3_out, and_4_out, nor_1_out, not_1_out, not_2_out, not_3_out, not_4_out,
       not_5_out, not_6_out, not_7_out, not_8_out, not_9_out;

  not not_1 (not_1_out, adress_bus_in[1]);
  not not_2 (not_2_out, adress_bus_in[2]);
  not not_3 (not_3_out, adress_bus_in[3]);
  not not_4 (not_4_out, adress_bus_in[0]);
  not not_5 (not_5_out, adress_bus_in[3]);
  not not_6 (not_6_out, adress_bus_in[2]);
  nor nor_1 (nor_1_out, adress_bus_in[3], adress_bus_in[2]);
  not not_7 (not_7_out, adress_bus_in[0]);
  not not_8 (not_8_out, adress_bus_in[1]);
  not not_9 (not_9_out, adress_bus_in[3]);
  and and_1 (and_1_out, adress_bus_in[0], not_1_out, not_2_out, not_3_out);
  and and_2 (and_2_out, not_4_out, adress_bus_in[1], not_5_out, not_6_out);
  and and_3 (and_3_out, nor_1_out, adress_bus_in[1], adress_bus_in[0]);
  and and_4 (and_4_out, adress_bus_in[2], not_7_out, not_8_out, not_9_out);
  and and_5 (adress_0, and_1_out, adress_bus_in[7]);
  and and_6 (adress_1, and_2_out, adress_bus_in[7]);
  and and_7 (adress_2, and_3_out, adress_bus_in[7]);
  and and_8 (adress_3, and_4_out, adress_bus_in[7]);
endmodule

module Adress_dcoder (
  input  [7:0] in_1,
  output adress_0,
  output adress_1,
  output adress_2,
  output adress_3
);

  wire nor_1_out, not_1_out, not_2_out, not_3_out, not_4_out, not_5_out, not_6_out;

  not not_1 (not_1_out, in_1[5]);
  not not_2 (not_2_out, in_1[6]);
  not not_3 (not_3_out, in_1[4]);
  not not_4 (not_4_out, in_1[6]);
  not nor_1 (nor_1_out, in_1[6]);  // NOR_Gate
  not not_5 (not_5_out, in_1[4]);
  not not_6 (not_6_out, in_1[5]);
  and and_1 (adress_0, in_1[4], not_1_out, not_2_out);
  and and_2 (adress_1, not_3_out, in_1[5], not_4_out);
  and and_3 (adress_2, nor_1_out, in_1[5], in_1[4]);
  and and_4 (adress_3, in_1[6], not_5_out, not_6_out);
endmodule

module read_to_self (
  input  [7:0] in_1
);
endmodule

module tmp (
  input  [7:0] adress_bus_in,
  output adress_0,
  output adress_1,
  output adress_2,
  output adress_3
);

  wire nor_1_out, not_1_out, not_2_out, not_3_out, not_4_out, not_5_out, not_6_out, not_7_out, not_8_out,
       not_9_out;

  not not_1 (not_1_out, adress_bus_in[1]);
  not not_2 (not_2_out, adress_bus_in[2]);
  not not_3 (not_3_out, adress_bus_in[3]);
  not not_4 (not_4_out, adress_bus_in[0]);
  not not_5 (not_5_out, adress_bus_in[3]);
  not not_6 (not_6_out, adress_bus_in[2]);
  nor nor_1 (nor_1_out, adress_bus_in[3], adress_bus_in[2]);
  not not_7 (not_7_out, adress_bus_in[0]);
  not not_8 (not_8_out, adress_bus_in[1]);
  not not_9 (not_9_out, adress_bus_in[3]);
  and and_1 (adress_0, adress_bus_in[0], not_1_out, not_2_out, not_3_out);
  and and_2 (adress_1, not_4_out, adress_bus_in[1], not_5_out, not_6_out);
  and and_3 (adress_2, nor_1_out, adress_bus_in[1], adress_bus_in[0]);
  and and_4 (adress_3, adress_bus_in[2], not_7_out, not_8_out, not_9_out);
endmodule

module Instruction_decoder (
  input  [7:0] in_1,
  output read_reg,
  output read_bus
);

  wire nor_1_out, nor_2_out;

  nor nor_1 (nor_1_out, in_1[7], in_1[6], in_1[5], in_1[4], in_1[3], in_1[2], in_1[0]);
  and and_1 (read_reg, nor_1_out, in_1[1]);
  and and_2 (read_bus, in_1[0], nor_2_out);
  nor nor_2 (nor_2_out, in_1[1], in_1[2], in_1[3], in_1[4], in_1[5], in_1[6], in_1[7]);
endmodule

module temp (
  input  [7:0] in_1,
  output out_2
);

  wire nor_1_out;

  nor nor_1 (nor_1_out, in_1[2], in_1[3], in_1[4], in_1[5], in_1[6], in_1[7]);
  and and_1 (out_2, in_1[0], in_1[1], nor_1_out);
endmodule

module comperater (
  input  [7:0] instruction_bus,
  input  [7:0] data_in
);

  wire and_1_out, and_2_out, and_3_out, and_4_out, and_5_out, and_6_out, and_7_out, and_8_out, nor_1_out,
       nor_2_out, nor_3_out, nor_4_out, nor_5_out, nor_6_out, nor_7_out, or_1_out;

  nor nor_1 (nor_1_out, instruction_bus[0], instruction_bus[2], instruction_bus[4], instruction_bus[5], instruction_bus[6], instruction_bus[7]);
  nor nor_2 (nor_2_out, instruction_bus[2], instruction_bus[4], instruction_bus[5], instruction_bus[6], instruction_bus[7]);
  nor nor_3 (nor_3_out, instruction_bus[4], instruction_bus[5], instruction_bus[6], instruction_bus[7], instruction_bus[1], instruction_bus[0]);
  nor nor_4 (nor_4_out, instruction_bus[4], instruction_bus[5], instruction_bus[6], instruction_bus[7], instruction_bus[1]);
  nor nor_5 (nor_5_out, instruction_bus[4], instruction_bus[5], instruction_bus[6], instruction_bus[7], instruction_bus[0]);
  nor nor_6 (nor_6_out, instruction_bus[4], instruction_bus[5], instruction_bus[6], instruction_bus[7]);
  and and_1 (and_1_out, instruction_bus[1], instruction_bus[3], nor_1_out);
  and and_2 (and_2_out, instruction_bus[1], instruction_bus[3], instruction_bus[0], nor_2_out);
  and and_3 (and_3_out, instruction_bus[3], instruction_bus[2], nor_3_out);
  and and_4 (and_4_out, instruction_bus[3], instruction_bus[0], instruction_bus[2], nor_4_out);
  and and_5 (and_5_out, instruction_bus[3], instruction_bus[2], instruction_bus[1], nor_5_out);
  and and_6 (and_6_out, instruction_bus[3], instruction_bus[2], instruction_bus[1], instruction_bus[0], nor_6_out);
  nor nor_7 (nor_7_out, data_in[0], data_in[1], data_in[2], data_in[3], data_in[4], data_in[5], data_in[6], data_in[7]);
  and and_7 (and_7_out, and_1_out, nor_7_out);
  or or_1 (or_1_out, data_in[0], data_in[1], data_in[2], data_in[3], data_in[4], data_in[5], data_in[6], data_in[7]);
  and and_8 (and_8_out, and_2_out, or_1_out);
endmodule

module alu_decoder (
  input  [7:0] instruction_Bus_in,
  output subtraction,
  output addition
);

  wire nor_1_out, nor_2_out;

  nor nor_1 (nor_1_out, instruction_Bus_in[7], instruction_Bus_in[6], instruction_Bus_in[5], instruction_Bus_in[4], instruction_Bus_in[3]);
  nor nor_2 (nor_2_out, instruction_Bus_in[0], instruction_Bus_in[3], instruction_Bus_in[4], instruction_Bus_in[5], instruction_Bus_in[6], instruction_Bus_in[7]);
  and and_1 (subtraction, nor_1_out, instruction_Bus_in[2], instruction_Bus_in[1], instruction_Bus_in[0]);
  and and_2 (addition, instruction_Bus_in[1], instruction_Bus_in[2], nor_2_out);
endmodule
